// Logisim project projeto_arcade.circ as structural Verilog: 53 circuits, main circuit main
module main (
);

  wire and_1_out, clock_1_out, Cls_out, not_1_out, or_1_out, Pause_out, R, S_out, Start_out, start_pause_1_q,
       ula_1_zero, unidade_controle_1_alusrc, unidade_controle_1_branch, unidade_controle_1_jump,
       unidade_controle_1_loadbuffer, unidade_controle_1_memoreg, unidade_controle_1_memwrite,
       unidade_controle_1_pcpause, unidade_controle_1_regwrite, unidade_controle_1_rgdst,
       unidade_controle_1_storegraphics;
  wire [1:0] unidade_controle_1_aluop;
  wire [2:0] aluctrl_1_out_3, multiplexador_2x3b_1_out;
  wire [6:0] keyboard_1_data;
  wire [15:0] add_16b_1_out_3, add_16b_2_out_3, extensor_1_16_1_out, extensor_6_16_1_out,
       extensor_07_16_1_out, extensor_12_16_1_out, memoria_grafica_1_out_1, memoria_grafica_1_out_2,
       memoria_grafica_1_out_3, memoria_grafica_1_out_4, memoria_grafica_1_out_5, memoria_grafica_1_out_6,
       memoria_grafica_1_out_7, memoria_grafica_1_out_8, multiplexador_2x16b_1_out,
       multiplexador_2x16b_2_out, multiplexador_2x16b_3_out, multiplexador_2x16b_4_out,
       multiplexador_2x16b_5_out, pc_1_out, ram_1_data, registers_1_out_1, registers_1_out_2, rom_1_data,
       ula_1_out;

  Button Start (.out(Start_out));
  Button Pause (.out(Pause_out));
  Button u_R (.out(R));
  or or_1 (or_1_out, Pause_out, unidade_controle_1_pcpause);
  Start_Pause start_pause_1 (.Start(Start_out), .Pause(or_1_out), .Q(start_pause_1_q));
  PC pc_1 (.Data(multiplexador_2x16b_2_out), .Out(pc_1_out), .CK(clock_1_out), .E(start_pause_1_q), .R(R), .S(S_out));
  Button S (.out(S_out));
  Clock #(.highDuration(2), .lowDuration(2)) clock_1 (.out(clock_1_out));
  Add_16b add_16b_1 (.A(pc_1_out), .B(extensor_1_16_1_out), .out_3(add_16b_1_out_3));
  Extensor_1_16 extensor_1_16_1 (.In(1'b1), .Out(extensor_1_16_1_out));
  ROM #(.addrWidth(16), .dataWidth(16)) rom_1 (.addr(pc_1_out), .data(rom_1_data), .sel(1'b1));
  Extensor_12_16 extensor_12_16_1 (.In(rom_1_data[11:0]), .Out(extensor_12_16_1_out));
  Unidade_Controle unidade_controle_1 (
    .OpCode(rom_1_data[15:12]), .RgDst(unidade_controle_1_rgdst), .MemoReg(unidade_controle_1_memoreg),
    .MemWrite(unidade_controle_1_memwrite), .AluOp(unidade_controle_1_aluop),
    .AluSrc(unidade_controle_1_alusrc), .RegWrite(unidade_controle_1_regwrite),
    .PcPause(unidade_controle_1_pcpause), .Branch(unidade_controle_1_branch), .Jump(unidade_controle_1_jump),
    .StoreGraphics(unidade_controle_1_storegraphics), .LoadBuffer(unidade_controle_1_loadbuffer));
  Multiplexador_2x3b multiplexador_2x3b_1 (
    ._0(rom_1_data[8:6]), ._1(rom_1_data[5:3]), .Out(multiplexador_2x3b_1_out), .Op(unidade_controle_1_rgdst));
  Extensor_6_16 extensor_6_16_1 (.In(rom_1_data[5:0]), .Out(extensor_6_16_1_out));
  Registers registers_1 (
    .R(R), .Clock(clock_1_out), .Enable_write(unidade_controle_1_regwrite),
    .Write_data(multiplexador_2x16b_4_out), .Rd(multiplexador_2x3b_1_out), .Rs(rom_1_data[11:9]),
    .Rt(rom_1_data[8:6]), .Out_1(registers_1_out_1), .Out_2(registers_1_out_2));
  Keyboard #(.buflen(8)) keyboard_1 (
    .clk(clock_1_out), .re(unidade_controle_1_loadbuffer), .clr(Cls_out), .data(keyboard_1_data));  // open: avail
  Button Cls (.out(Cls_out));
  Add_16b add_16b_2 (.A(add_16b_1_out_3), .B(extensor_6_16_1_out), .out_3(add_16b_2_out_3));
  and and_1 (and_1_out, unidade_controle_1_branch, ula_1_zero);
  Multiplexador_2x16b multiplexador_2x16b_1 (
    ._0(registers_1_out_2), ._1(extensor_6_16_1_out), .Out(multiplexador_2x16b_1_out),
    .Op(unidade_controle_1_alusrc));  // open: Op_2
  AluCtrl aluctrl_1 (.AluOp(unidade_controle_1_aluop), .Funct(rom_1_data[2:0]), .out_3(aluctrl_1_out_3));
  Multiplexador_2x16b multiplexador_2x16b_2 (
    ._0(multiplexador_2x16b_3_out), ._1(extensor_12_16_1_out), .Out(multiplexador_2x16b_2_out),
    .Op_2(unidade_controle_1_jump));  // open: Op
  Multiplexador_2x16b multiplexador_2x16b_3 (
    ._0(add_16b_1_out_3), ._1(add_16b_2_out_3), .Out(multiplexador_2x16b_3_out), .Op_2(and_1_out));  // open: Op
  ULA ula_1 (
    .A(registers_1_out_1), .B(multiplexador_2x16b_1_out), .Out(ula_1_out), .Funct(aluctrl_1_out_3),
    .Zero(ula_1_zero));
  Multiplexador_2x16b multiplexador_2x16b_4 (
    ._0(multiplexador_2x16b_5_out), ._1(extensor_07_16_1_out), .Out(multiplexador_2x16b_4_out),
    .Op_2(unidade_controle_1_loadbuffer));  // open: Op
  Memoria_grafica memoria_grafica_1 (
    .R(R), .Clock(clock_1_out), .Write_data(registers_1_out_2),
    .Enable_write(unidade_controle_1_storegraphics), .Address(ula_1_out[2:0]),
    .Out_1(memoria_grafica_1_out_1), .Out_2(memoria_grafica_1_out_2), .Out_3(memoria_grafica_1_out_3),
    .Out_4(memoria_grafica_1_out_4), .Out_5(memoria_grafica_1_out_5), .Out_6(memoria_grafica_1_out_6),
    .Out_7(memoria_grafica_1_out_7), .Out_8(memoria_grafica_1_out_8));
  Extensor_07_16 extensor_07_16_1 (.In(keyboard_1_data), .Out(extensor_07_16_1_out));
  DotMatrix #(.inputtype("row"), .matrixcols(16), .matrixrows(8)) dotmatrix_1 (
    .row0(memoria_grafica_1_out_1), .row1(memoria_grafica_1_out_2), .row2(memoria_grafica_1_out_3),
    .row3(memoria_grafica_1_out_4), .row4(memoria_grafica_1_out_5), .row5(memoria_grafica_1_out_6),
    .row6(memoria_grafica_1_out_7), .row7(memoria_grafica_1_out_8));
  not not_1 (not_1_out, unidade_controle_1_memwrite);
  RAM_part #(.addrWidth(16), .dataWidth(16), .bus("separate")) ram_1 (
    .addr(ula_1_out), .din(registers_1_out_2), .data(ram_1_data), .str(unidade_controle_1_memwrite),
    .sel(1'b1), .clk(clock_1_out), .ld(not_1_out), .clr(R));
  Multiplexador_2x16b multiplexador_2x16b_5 (
    ._0(ram_1_data), ._1(ula_1_out), .Out(multiplexador_2x16b_5_out), .Op(unidade_controle_1_memoreg));  // open: Op_2

  // Notes on the sheet:
  //   contents of rom_1 (hex, n*v repeats v):
  //   1040 1081 10c2 1103 3141 3180 9d40 a1c0 5e41 600d 9c00 4d81 6006 5e81 6013 3001 a2f 4001 6006 5f01
  //   6019 3001 a2e 4001 6006 5ec1 6006 9c00 3d81 6006 f000
endmodule

module Micro_CPU_16b (
  input  Start,
  input  Pause,
  input  Reset,
  input  [6:0] Keyboard,
  input  Clock,
  output [15:0] Graphics,
  output [15:0] Graphics_2,
  output [15:0] Graphics_3,
  output [15:0] Graphics_4,
  output [15:0] Graphics_5,
  output [15:0] Graphics_6,
  output [15:0] Graphics_7,
  output [15:0] Graphics_8,
  output Select_KB
);

  wire and_1_out, not_1_out, or_1_out, S_out, start_pause_1_q, ula_1_zero, unidade_controle_1_alusrc,
       unidade_controle_1_branch, unidade_controle_1_jump, unidade_controle_1_memoreg,
       unidade_controle_1_memwrite, unidade_controle_1_pcpause, unidade_controle_1_regwrite,
       unidade_controle_1_rgdst, unidade_controle_1_storegraphics;
  wire [1:0] unidade_controle_1_aluop;
  wire [2:0] aluctrl_1_out_3, multiplexador_2x3b_1_out;
  wire [15:0] add_16b_1_out_3, add_16b_2_out_3, extensor_1_16_1_out, extensor_6_16_1_out,
       extensor_07_16_1_out, extensor_12_16_1_out, multiplexador_2x16b_1_out, multiplexador_2x16b_2_out,
       multiplexador_2x16b_3_out, multiplexador_2x16b_4_out, multiplexador_2x16b_5_out, pc_1_out, ram_1_data,
       registers_1_out_1, registers_1_out_2, rom_1_data, ula_1_out;

  or or_1 (or_1_out, Pause, unidade_controle_1_pcpause);
  Start_Pause start_pause_1 (.Start(Start), .Pause(or_1_out), .Q(start_pause_1_q));
  PC pc_1 (.Data(multiplexador_2x16b_3_out), .Out(pc_1_out), .CK(Clock), .E(start_pause_1_q), .R(Reset), .S(S_out));
  Button S (.out(S_out));
  Add_16b add_16b_1 (.A(pc_1_out), .B(extensor_1_16_1_out), .out_3(add_16b_1_out_3));
  Extensor_1_16 extensor_1_16_1 (.In(1'b1), .Out(extensor_1_16_1_out));
  ROM #(.addrWidth(16), .dataWidth(16)) rom_1 (.addr(pc_1_out), .data(rom_1_data), .sel(1'b1));
  Extensor_12_16 extensor_12_16_1 (.In(rom_1_data[11:0]), .Out(extensor_12_16_1_out));
  Unidade_Controle unidade_controle_1 (
    .OpCode(rom_1_data[15:12]), .RgDst(unidade_controle_1_rgdst), .MemoReg(unidade_controle_1_memoreg),
    .MemWrite(unidade_controle_1_memwrite), .AluOp(unidade_controle_1_aluop),
    .AluSrc(unidade_controle_1_alusrc), .RegWrite(unidade_controle_1_regwrite),
    .PcPause(unidade_controle_1_pcpause), .Branch(unidade_controle_1_branch), .Jump(unidade_controle_1_jump),
    .StoreGraphics(unidade_controle_1_storegraphics), .LoadBuffer(Select_KB));
  Multiplexador_2x3b multiplexador_2x3b_1 (
    ._0(rom_1_data[8:6]), ._1(rom_1_data[5:3]), .Out(multiplexador_2x3b_1_out), .Op(unidade_controle_1_rgdst));
  Extensor_6_16 extensor_6_16_1 (.In(rom_1_data[5:0]), .Out(extensor_6_16_1_out));
  Registers registers_1 (
    .R(Reset), .Clock(Clock), .Enable_write(unidade_controle_1_regwrite),
    .Write_data(multiplexador_2x16b_4_out), .Rd(multiplexador_2x3b_1_out), .Rs(rom_1_data[11:9]),
    .Rt(rom_1_data[8:6]), .Out_1(registers_1_out_1), .Out_2(registers_1_out_2));
  Add_16b add_16b_2 (.A(add_16b_1_out_3), .B(extensor_6_16_1_out), .out_3(add_16b_2_out_3));
  and and_1 (and_1_out, unidade_controle_1_branch, ula_1_zero);
  Multiplexador_2x16b multiplexador_2x16b_1 (
    ._0(registers_1_out_2), ._1(extensor_6_16_1_out), .Out(multiplexador_2x16b_1_out),
    .Op(unidade_controle_1_alusrc));  // open: Op_2
  AluCtrl aluctrl_1 (.AluOp(unidade_controle_1_aluop), .Funct(rom_1_data[2:0]), .out_3(aluctrl_1_out_3));
  Multiplexador_2x16b multiplexador_2x16b_2 (
    ._0(add_16b_1_out_3), ._1(add_16b_2_out_3), .Out(multiplexador_2x16b_2_out), .Op_2(and_1_out));  // open: Op
  Multiplexador_2x16b multiplexador_2x16b_3 (
    ._0(multiplexador_2x16b_2_out), ._1(extensor_12_16_1_out), .Out(multiplexador_2x16b_3_out),
    .Op_2(unidade_controle_1_jump));  // open: Op
  ULA ula_1 (
    .A(registers_1_out_1), .B(multiplexador_2x16b_1_out), .Out(ula_1_out), .Funct(aluctrl_1_out_3),
    .Zero(ula_1_zero));
  Multiplexador_2x16b multiplexador_2x16b_4 (
    ._0(multiplexador_2x16b_5_out), ._1(extensor_07_16_1_out), .Out(multiplexador_2x16b_4_out),
    .Op_2(Select_KB));  // open: Op
  Memoria_grafica memoria_grafica_1 (
    .R(Reset), .Clock(Clock), .Write_data(registers_1_out_2),
    .Enable_write(unidade_controle_1_storegraphics), .Address(ula_1_out[2:0]), .Out_1(Graphics),
    .Out_2(Graphics_2), .Out_3(Graphics_3), .Out_4(Graphics_4), .Out_5(Graphics_5), .Out_6(Graphics_6),
    .Out_7(Graphics_7), .Out_8(Graphics_8));
  Extensor_07_16 extensor_07_16_1 (.In(Keyboard), .Out(extensor_07_16_1_out));
  not not_1 (not_1_out, unidade_controle_1_memwrite);
  RAM_part #(.addrWidth(16), .dataWidth(16), .bus("separate")) ram_1 (
    .addr(ula_1_out), .din(registers_1_out_2), .data(ram_1_data), .str(unidade_controle_1_memwrite),
    .sel(1'b1), .clk(Clock), .ld(not_1_out), .clr(Reset));
  Multiplexador_2x16b multiplexador_2x16b_5 (
    ._0(ram_1_data), ._1(ula_1_out), .Out(multiplexador_2x16b_5_out), .Op(unidade_controle_1_memoreg));  // open: Op_2

  // Other names for the same wires on the sheet: R = Reset

  // Notes on the sheet:
  //   Clock: pull=down
  //   Graphics_7: pull=down
  //   Graphics_2: pull=down
  //   Graphics_5: pull=down
  //   Graphics: pull=down
  //   Reset: pull=down
  //   Keyboard: pull=down
  //   Graphics_6: pull=down
  //   Pause: pull=down
  //   Graphics_4: pull=down
  //   Graphics_3: pull=down
  //   Graphics_8: pull=down
  //   Select_KB: pull=down
  //   Start: pull=down
  //   contents of rom_1 (hex, n*v repeats v):
  //   3041 3081 30cf 2de 9080 456 9080 54c1 6005 9041 f000
endmodule

module Testes (
);

  wire clock_1_out, micro_cpu_16b_1_select_kb, Pause_out, R_out, Start_out;
  wire [6:0] keyboard_1_data;
  wire [15:0] micro_cpu_16b_1_graphics, micro_cpu_16b_1_graphics_2, micro_cpu_16b_1_graphics_3,
       micro_cpu_16b_1_graphics_4, micro_cpu_16b_1_graphics_5, micro_cpu_16b_1_graphics_6,
       micro_cpu_16b_1_graphics_7, micro_cpu_16b_1_graphics_8;

  Clock #(.highDuration(2), .lowDuration(2)) clock_1 (.out(clock_1_out));
  Keyboard #(.buflen(8)) keyboard_1 (
    .clk(clock_1_out), .re(micro_cpu_16b_1_select_kb), .data(keyboard_1_data));  // open: clr, avail
  Button Start (.out(Start_out));
  Button Pause (.out(Pause_out));
  Button R (.out(R_out));
  DotMatrix #(.matrixcols(8), .matrixrows(16)) dotmatrix_1 (
    .col0(micro_cpu_16b_1_graphics), .col1(micro_cpu_16b_1_graphics_2), .col2(micro_cpu_16b_1_graphics_3),
    .col3(micro_cpu_16b_1_graphics_4), .col4(micro_cpu_16b_1_graphics_5), .col5(micro_cpu_16b_1_graphics_6),
    .col6(micro_cpu_16b_1_graphics_7), .col7(micro_cpu_16b_1_graphics_8));
  Micro_CPU_16b micro_cpu_16b_1 (
    .Reset(R_out), .Keyboard(keyboard_1_data), .Select_KB(micro_cpu_16b_1_select_kb), .Start(Start_out),
    .Graphics(micro_cpu_16b_1_graphics), .Pause(Pause_out), .Graphics_2(micro_cpu_16b_1_graphics_2),
    .Graphics_3(micro_cpu_16b_1_graphics_3), .Graphics_4(micro_cpu_16b_1_graphics_4),
    .Graphics_5(micro_cpu_16b_1_graphics_5), .Graphics_6(micro_cpu_16b_1_graphics_6),
    .Graphics_7(micro_cpu_16b_1_graphics_7), .Graphics_8(micro_cpu_16b_1_graphics_8), .Clock(clock_1_out));
endmodule

module Memoria_8x8b (
  input  [2:0] Andress,
  input  [7:0] Data,
  input  Cl,
  input  W,
  input  S,
  input  R,
  output [7:0] Out
);

  wire and_1_out, multi_a_men_8b_1__0, multi_a_men_8b_1__1, multi_a_men_8b_1__2, multi_a_men_8b_1__3,
       multi_a_men_8b_1__4, multi_a_men_8b_1__5, multi_a_men_8b_1__6, multi_a_men_8b_1__7;
  wire [7:0] _0_out, _1_out, _2_out, _3_out, _4_out, _5_out, _6_out, _7_out;

  Multi_A_Men_8b multi_a_men_8b_1 (
    .in_1(Andress), ._0(multi_a_men_8b_1__0), ._1(multi_a_men_8b_1__1), ._2(multi_a_men_8b_1__2),
    ._3(multi_a_men_8b_1__3), ._4(multi_a_men_8b_1__4), ._5(multi_a_men_8b_1__5), ._6(multi_a_men_8b_1__6),
    ._7(multi_a_men_8b_1__7));
  and and_1 (and_1_out, Cl, W);
  Palavra_8b _7 (.Data(Data), .Out(_7_out), .CK(and_1_out), .E(multi_a_men_8b_1__7), .R(R), .S(S));
  Palavra_8b _6 (.Data(Data), .Out(_6_out), .CK(and_1_out), .E(multi_a_men_8b_1__6), .R(R), .S(S));
  Palavra_8b _5 (.Data(Data), .Out(_5_out), .CK(and_1_out), .E(multi_a_men_8b_1__5), .R(R), .S(S));
  Palavra_8b _4 (.Data(Data), .Out(_4_out), .CK(and_1_out), .E(multi_a_men_8b_1__4), .R(R), .S(S));
  Palavra_8b _3 (.Data(Data), .Out(_3_out), .CK(and_1_out), .E(multi_a_men_8b_1__3), .R(R), .S(S));
  Palavra_8b _2 (.Data(Data), .Out(_2_out), .CK(and_1_out), .E(multi_a_men_8b_1__2), .R(R), .S(S));
  Palavra_8b _1 (.Data(Data), .Out(_1_out), .CK(and_1_out), .E(multi_a_men_8b_1__1), .R(R), .S(S));
  Palavra_8b _0 (.Data(Data), .Out(_0_out), .CK(and_1_out), .E(multi_a_men_8b_1__0), .R(R), .S(S));
  Multi_B_Men_8b multi_b_men_8b_1 (
    ._7(_7_out), ._6(_6_out), ._5(_5_out), ._4(_4_out), ._3(_3_out), ._2(_2_out), ._1(_1_out), ._0(_0_out),
    .out_10(Out), .in_1(Andress));

  // Notes on the sheet:
  //   Out: pull=down
  //   Data: pull=down
  //   Andress: pull=down
  //   Cl: pull=down
  //   S: pull=down
  //   W: pull=down
  //   R: pull=down
endmodule

module Multi_A_Men_8b (
  input  [2:0] in_1,
  output _0,
  output _1,
  output _2,
  output _3,
  output _4,
  output _5,
  output _6,
  output _7
);

  and and_1 (_0, ~in_1[2], ~in_1[1], ~in_1[0]);  // AND_Gate
  and and_2 (_1, ~in_1[2], ~in_1[1], in_1[0]);  // AND_Gate
  and and_3 (_2, ~in_1[2], in_1[1], ~in_1[0]);  // AND_Gate
  and and_4 (_3, ~in_1[2], in_1[1], in_1[0]);  // AND_Gate
  and and_5 (_4, in_1[2], ~in_1[1], ~in_1[0]);  // AND_Gate
  and and_6 (_5, in_1[2], ~in_1[1], in_1[0]);  // AND_Gate
  and and_7 (_6, in_1[2], in_1[1], ~in_1[0]);  // AND_Gate
  and and_8 (_7, in_1[2], in_1[1], in_1[0]);

  // Notes on the sheet:
  //   _6: pull=down
  //   _0: pull=down
  //   _3: pull=down
  //   _1: pull=down
  //   in_1: pull=down
  //   _2: pull=down
  //   _5: pull=down
  //   _4: pull=down
  //   _7: pull=down
endmodule

module Multi_B_Men_8b (
  input  [2:0] in_1,
  input  [7:0] _7,
  input  [7:0] _6,
  input  [7:0] _5,
  input  [7:0] _4,
  input  [7:0] _3,
  input  [7:0] _2,
  input  [7:0] _1,
  input  [7:0] _0,
  output [7:0] out_10
);

  wire multi_a_men_8b_1__0, multi_a_men_8b_1__1, multi_a_men_8b_1__2, multi_a_men_8b_1__3,
       multi_a_men_8b_1__4, multi_a_men_8b_1__5, multi_a_men_8b_1__6, multi_a_men_8b_1__7;
  wire [7:0] select_8b_1_out, select_8b_2_out, select_8b_3_out, select_8b_4_out, select_8b_5_out,
       select_8b_6_out, select_8b_7_out, select_8b_8_out;

  Multi_A_Men_8b multi_a_men_8b_1 (
    .in_1(in_1), ._0(multi_a_men_8b_1__0), ._1(multi_a_men_8b_1__1), ._2(multi_a_men_8b_1__2),
    ._3(multi_a_men_8b_1__3), ._4(multi_a_men_8b_1__4), ._5(multi_a_men_8b_1__5), ._6(multi_a_men_8b_1__6),
    ._7(multi_a_men_8b_1__7));
  Select_8b select_8b_1 (.E(multi_a_men_8b_1__7), .In(_7), .Out(select_8b_1_out));
  Select_8b select_8b_2 (.E(multi_a_men_8b_1__6), .In(_6), .Out(select_8b_2_out));
  Select_8b select_8b_3 (.E(multi_a_men_8b_1__5), .In(_5), .Out(select_8b_3_out));
  Select_8b select_8b_4 (.E(multi_a_men_8b_1__4), .In(_4), .Out(select_8b_4_out));
  Select_8b select_8b_5 (.E(multi_a_men_8b_1__3), .In(_3), .Out(select_8b_5_out));
  Select_8b select_8b_6 (.E(multi_a_men_8b_1__2), .In(_2), .Out(select_8b_6_out));
  Select_8b select_8b_7 (.E(multi_a_men_8b_1__1), .In(_1), .Out(select_8b_7_out));
  Select_8b select_8b_8 (.E(multi_a_men_8b_1__0), .In(_0), .Out(select_8b_8_out));
  OR_Men_8b or_men_8b_1 (
    .out_9(out_10), .in_1(select_8b_8_out), .in_2(select_8b_7_out), .in_3(select_8b_6_out),
    .in_4(select_8b_5_out), .in_5(select_8b_4_out), .in_6(select_8b_3_out), .in_7(select_8b_2_out),
    .in_8(select_8b_1_out));

  // Notes on the sheet:
  //   _2: pull=down
  //   _7: pull=down
  //   _5: pull=down
  //   _6: pull=down
  //   _4: pull=down
  //   _1: pull=down
  //   _3: pull=down
  //   in_1: pull=down
  //   out_10: pull=down
  //   _0: pull=down
endmodule

module Select_8b (
  input  E,
  input  [7:0] In,
  output [7:0] Out
);

  and and_1 (Out[0], E, In[0]);
  and and_2 (Out[1], E, In[1]);
  and and_3 (Out[2], E, In[2]);
  and and_4 (Out[3], E, In[3]);
  and and_5 (Out[4], In[4], E);
  and and_6 (Out[5], In[5], E);
  and and_7 (Out[6], In[6], E);
  and and_8 (Out[7], In[7], E);

  // Notes on the sheet:
  //   In: pull=down
  //   E: pull=down
  //   Out: pull=down
endmodule

module OR_Men_8b (
  input  [7:0] in_1,
  input  [7:0] in_2,
  input  [7:0] in_3,
  input  [7:0] in_4,
  input  [7:0] in_5,
  input  [7:0] in_6,
  input  [7:0] in_7,
  input  [7:0] in_8,
  output [7:0] out_9
);

  or or_1 (out_9[0], in_1[0], in_2[0], in_3[0], in_4[0], in_5[0], in_6[0], in_7[0], in_8[0]);
  or or_2 (out_9[1], in_1[1], in_2[1], in_3[1], in_4[1], in_5[1], in_6[1], in_7[1], in_8[1]);
  or or_3 (out_9[2], in_1[2], in_2[2], in_3[2], in_4[2], in_5[2], in_6[2], in_7[2], in_8[2]);
  or or_4 (out_9[3], in_1[3], in_2[3], in_3[3], in_4[3], in_5[3], in_6[3], in_7[3], in_8[3]);
  or or_5 (out_9[4], in_1[4], in_2[4], in_3[4], in_4[4], in_5[4], in_6[4], in_7[4], in_8[4]);
  or or_6 (out_9[5], in_1[5], in_2[5], in_3[5], in_4[5], in_5[5], in_6[5], in_7[5], in_8[5]);
  or or_7 (out_9[6], in_1[6], in_2[6], in_3[6], in_4[6], in_5[6], in_6[6], in_7[6], in_8[6]);
  or or_8 (out_9[7], in_1[7], in_2[7], in_3[7], in_4[7], in_5[7], in_6[7], in_7[7], in_8[7]);

  // Notes on the sheet:
  //   in_7: pull=down
  //   in_2: pull=down
  //   in_6: pull=down
  //   in_8: pull=down
  //   in_1: pull=down
  //   out_9: pull=down
  //   in_3: pull=down
  //   in_4: pull=down
  //   in_5: pull=down
endmodule

module Ctrl_Display_Ate_9 (
  input  [3:0] in_1,
  output _0,
  output _1,
  output _2,
  output _3,
  output _4,
  output _5,
  output _6,
  output _7
);

  wire and_1_out, and_2_out, and_3_out, and_4_out, and_5_out, and_6_out, and_7_out, and_8_out, and_9_out,
       and_10_out, and_11_out, and_12_out, and_13_out, and_14_out, and_15_out, and_16_out;

  and and_1 (and_1_out, ~in_1[1], ~in_1[0]);  // AND_Gate
  and and_2 (and_2_out, in_1[0], in_1[1]);
  and and_3 (and_3_out, ~in_1[2], ~in_1[0]);  // AND_Gate
  and and_4 (and_4_out, in_1[2], in_1[0]);
  and and_5 (and_5_out, ~in_1[1], ~in_1[0]);  // AND_Gate
  and and_6 (and_6_out, in_1[2], ~in_1[1]);  // AND_Gate
  and and_7 (and_7_out, in_1[2], ~in_1[0]);  // AND_Gate
  and and_8 (and_8_out, ~in_1[2], in_1[1]);  // AND_Gate
  and and_9 (and_9_out, in_1[1], ~in_1[0]);  // AND_Gate
  and and_10 (and_10_out, in_1[2], ~in_1[1]);  // AND_Gate
  and and_11 (and_11_out, ~in_1[2], ~in_1[0]);  // AND_Gate
  and and_12 (and_12_out, ~in_1[2], in_1[1]);  // AND_Gate
  and and_13 (and_13_out, in_1[1], ~in_1[0]);  // AND_Gate
  and and_14 (and_14_out, in_1[2], ~in_1[1], in_1[0]);  // AND_Gate
  and and_15 (and_15_out, ~in_1[2], ~in_1[0]);  // AND_Gate
  and and_16 (and_16_out, in_1[1], ~in_1[0]);  // AND_Gate
  or or_1 (_0, and_1_out, ~in_1[2], and_2_out);  // OR_Gate
  or or_2 (_1, in_1[3], in_1[1], and_3_out, and_4_out);
  or or_3 (_2, in_1[3], and_5_out, and_6_out, and_7_out);
  or or_4 (_3, in_1[3], and_8_out, and_9_out, and_10_out);
  or or_5 (_5, ~in_1[1], in_1[0], in_1[2]);  // OR_Gate
  or or_6 (_6, in_1[3], and_11_out, and_12_out, and_13_out, and_14_out);
  or or_7 (_7, and_15_out, and_16_out);
  Button button_1 (.out(_4));

  // Notes on the sheet:
  //   _2: pull=down
  //   _0: pull=down
  //   _1: pull=down
  //   in_1: pull=down
  //   _7: pull=down
  //   _4: pull=down
  //   _3: pull=down
  //   _5: pull=down
  //   _6: pull=down
endmodule

module Add (
  input  A,
  input  B,
  input  Of_in,
  output Of_out,
  output Out
);

  wire and_1_out, and_2_out, and_3_out, and_4_out, and_5_out, and_6_out, and_7_out;

  and and_1 (and_1_out, A, B);
  and and_2 (and_2_out, Of_in, B);
  and and_3 (and_3_out, Of_in, A);
  and and_4 (and_4_out, ~Of_in, ~A, B);  // AND_Gate
  and and_5 (and_5_out, ~Of_in, A, ~B);  // AND_Gate
  and and_6 (and_6_out, Of_in, ~A, ~B);  // AND_Gate
  and and_7 (and_7_out, Of_in, A, B);
  or or_1 (Of_out, and_1_out, and_2_out, and_3_out);
  or or_2 (Out, and_4_out, and_5_out, and_6_out, and_7_out);

  // Notes on the sheet:
  //   Of_out: pull=down
  //   Out: pull=down
  //   B: pull=down
  //   Of_in: pull=down
  //   A: pull=down
endmodule

module Somador (
  input  [7:0] A,
  input  [7:0] B,
  output [7:0] Out
);

  wire add_1_of_out, add_2_of_out, add_3_of_out, add_4_of_out, add_5_of_out, add_6_of_out, add_7_of_out,
       add_8_of_out, button_1_out;

  Add add_1 (.B(B[0]), .A(A[0]), .Of_in(button_1_out), .Of_out(add_1_of_out), .Out(Out[0]));
  Button button_1 (.out(button_1_out));
  Add add_2 (.B(B[1]), .A(A[1]), .Of_in(add_1_of_out), .Of_out(add_2_of_out), .Out(Out[1]));
  Add add_3 (.B(B[2]), .A(A[2]), .Of_in(add_2_of_out), .Of_out(add_3_of_out), .Out(Out[2]));
  Add add_4 (.B(B[3]), .A(A[3]), .Of_in(add_3_of_out), .Of_out(add_4_of_out), .Out(Out[3]));
  Add add_5 (.B(B[4]), .A(A[4]), .Of_in(add_4_of_out), .Of_out(add_5_of_out), .Out(Out[4]));
  Add add_6 (.B(B[5]), .A(A[5]), .Of_in(add_5_of_out), .Of_out(add_6_of_out), .Out(Out[5]));
  Add add_7 (.B(B[6]), .A(A[6]), .Of_in(add_6_of_out), .Of_out(add_7_of_out), .Out(Out[6]));
  LED led_1 (.in(add_8_of_out));
  Add add_8 (.B(B[7]), .A(A[7]), .Of_in(add_7_of_out), .Of_out(add_8_of_out), .Out(Out[7]));

  // Notes on the sheet:
  //   A: pull=down
  //   Out: pull=down
  //   B: pull=down
endmodule

module Ctrl_Display (
  input  [3:0] in_1,
  output _0,
  output _1,
  output _2,
  output _3,
  output _4,
  output _5,
  output _6,
  output _7
);

  wire and_1_out, and_2_out, and_3_out, and_4_out, and_5_out, and_6_out, and_7_out, and_8_out, and_9_out,
       and_10_out, and_11_out, and_12_out, and_13_out, and_14_out, and_15_out, and_16_out, and_17_out,
       and_18_out, and_19_out;

  and and_1 (and_1_out, ~in_1[0], ~in_1[1]);  // AND_Gate
  and and_2 (and_2_out, in_1[0], in_1[1]);
  and and_3 (and_3_out, in_1[0], in_1[2]);
  and and_4 (and_4_out, ~in_1[0], ~in_1[2]);  // AND_Gate
  and and_5 (and_5_out, ~in_1[1], ~in_1[0]);  // AND_Gate
  and and_6 (and_6_out, ~in_1[1], in_1[2]);  // AND_Gate
  and and_7 (and_7_out, in_1[2], ~in_1[0]);  // AND_Gate
  and and_8 (and_8_out, ~in_1[3], ~in_1[2], in_1[1]);  // AND_Gate
  and and_9 (and_9_out, ~in_1[3], ~in_1[0], in_1[1]);  // AND_Gate
  and and_10 (and_10_out, ~in_1[3], ~in_1[1], in_1[2]);  // AND_Gate
  and and_11 (and_11_out, ~in_1[1], ~in_1[2], in_1[3]);  // AND_Gate
  and and_12 (and_12_out, ~in_1[2], ~in_1[0]);  // AND_Gate
  and and_13 (and_13_out, in_1[1], ~in_1[2]);  // AND_Gate
  and and_14 (and_14_out, in_1[1], ~in_1[0]);  // AND_Gate
  and and_15 (and_15_out, in_1[2], ~in_1[1], in_1[0]);  // AND_Gate
  and and_16 (and_16_out, ~in_1[2], ~in_1[0]);  // AND_Gate
  and and_17 (and_17_out, in_1[1], ~in_1[0]);  // AND_Gate
  and and_18 (and_18_out, in_1[3], in_1[1]);
  and and_19 (and_19_out, in_1[3], in_1[2]);
  or or_1 (_0, ~in_1[2], in_1[3], and_1_out, and_2_out);  // OR_Gate
  or or_2 (_1, in_1[1], in_1[3], and_3_out, and_4_out);
  or or_3 (_2, in_1[3], and_5_out, and_6_out, and_7_out);
  or or_4 (_3, and_8_out, and_9_out, and_10_out, and_11_out);
  or or_5 (_5, ~in_1[1], in_1[0], in_1[2], in_1[3]);  // OR_Gate
  or or_6 (_6, in_1[3], and_12_out, and_13_out, and_14_out, and_15_out);
  or or_7 (_7, and_16_out, and_17_out, and_18_out, and_19_out);
  Button button_1 (.out(_4));

  // Notes on the sheet:
  //   in_1: pull=down
  //   _6: pull=down
  //   _3: pull=down
  //   _2: pull=down
  //   _4: pull=down
  //   _5: pull=down
  //   _1: pull=down
  //   _7: pull=down
  //   _0: pull=down
endmodule

module Memoria_16x16b (
  input  S,
  input  R,
  input  Cl,
  input  W,
  input  [15:0] Data,
  input  [3:0] Andress,
  output [15:0] Out
);

  wire and_1_out;
  wire [7:0] multi_a_men_16_1_out_2;
  wire [15:0] _0, _1, _2, _3, _4, _5, _6, _7, _8, _9, A, B, C, D, E, F;
  wire [15:8] multi_a_men_16_1_out_2_2;

  Multi_A_Men_16 multi_a_men_16_1 (.in_1(Andress), .out_2({multi_a_men_16_1_out_2_2, multi_a_men_16_1_out_2}));
  and and_1 (and_1_out, Cl, W);
  Palavra_16b palavra_16b_1 (.Data(Data), .CK(and_1_out), .E(multi_a_men_16_1_out_2[0]), .R(R), .S(S), .Out(_0));
  Palavra_16b palavra_16b_2 (.Data(Data), .CK(and_1_out), .E(multi_a_men_16_1_out_2_2[8]), .R(R), .S(S), .Out(_8));
  Multi_B_Men_16b multi_b_men_16b_1 (
    ._15(F), ._14(E), ._13(D), ._12(C), ._11(B), ._10(A), ._9(_9), ._8(_8), ._7(_7), ._6(_6), ._5(_5),
    ._4(_4), ._3(_3), ._2(_2), ._1(_1), ._0(_0), .Adress(Andress), .Out(Out));
  Palavra_16b palavra_16b_3 (.Data(Data), .CK(and_1_out), .E(multi_a_men_16_1_out_2[1]), .R(R), .S(S), .Out(_1));
  Palavra_16b palavra_16b_4 (.Data(Data), .CK(and_1_out), .E(multi_a_men_16_1_out_2_2[9]), .R(R), .S(S), .Out(_9));
  Palavra_16b palavra_16b_5 (.Data(Data), .CK(and_1_out), .E(multi_a_men_16_1_out_2[2]), .R(R), .S(S), .Out(_2));
  Palavra_16b palavra_16b_6 (.Data(Data), .CK(and_1_out), .E(multi_a_men_16_1_out_2_2[10]), .R(R), .S(S), .Out(A));
  Palavra_16b palavra_16b_7 (.Data(Data), .CK(and_1_out), .E(multi_a_men_16_1_out_2[3]), .R(R), .S(S), .Out(_3));
  Palavra_16b palavra_16b_8 (.Data(Data), .CK(and_1_out), .E(multi_a_men_16_1_out_2_2[11]), .R(R), .S(S), .Out(B));
  Palavra_16b palavra_16b_9 (.Data(Data), .CK(and_1_out), .E(multi_a_men_16_1_out_2[4]), .R(R), .S(S), .Out(_4));
  Palavra_16b palavra_16b_10 (.Data(Data), .CK(and_1_out), .E(multi_a_men_16_1_out_2_2[12]), .R(R), .S(S), .Out(C));
  Palavra_16b palavra_16b_11 (.Data(Data), .CK(and_1_out), .E(multi_a_men_16_1_out_2[5]), .R(R), .S(S), .Out(_5));
  Palavra_16b palavra_16b_12 (.Data(Data), .CK(and_1_out), .E(multi_a_men_16_1_out_2_2[13]), .R(R), .S(S), .Out(D));
  Palavra_16b palavra_16b_13 (.Data(Data), .CK(and_1_out), .E(multi_a_men_16_1_out_2[6]), .R(R), .S(S), .Out(_6));
  Palavra_16b palavra_16b_14 (.Data(Data), .CK(and_1_out), .E(multi_a_men_16_1_out_2_2[14]), .R(R), .S(S), .Out(E));
  Palavra_16b palavra_16b_15 (.Data(Data), .CK(and_1_out), .E(multi_a_men_16_1_out_2[7]), .R(R), .S(S), .Out(_7));
  Palavra_16b palavra_16b_16 (.Data(Data), .CK(and_1_out), .E(multi_a_men_16_1_out_2_2[15]), .R(R), .S(S), .Out(F));

  // Notes on the sheet:
  //   Andress: pull=down
  //   W: pull=down
  //   R: pull=down
  //   Cl: pull=down
  //   Data: pull=down
  //   S: pull=down
  //   Out: pull=down
endmodule

module Palavra_16b (
  input  [15:0] Data,
  input  CK,
  input  E,
  input  R,
  input  S,
  output [15:0] Out
);

  wire and_1_out, and_2_out, and_3_out, and_4_out, and_5_out, and_6_out, and_7_out, and_8_out, and_9_out,
       and_10_out, and_11_out, and_12_out, and_13_out, and_14_out, and_15_out, and_16_out, and_17_out,
       and_18_out, and_19_out, and_20_out, and_21_out, and_22_out, and_23_out, and_24_out, and_25_out,
       and_26_out, and_27_out, and_28_out, and_29_out, and_30_out, and_31_out, and_32_out, and_33_out,
       and_34_out, and_35_out, and_36_out, and_37_out, and_38_out, and_39_out, and_40_out, and_41_out,
       and_42_out, and_43_out, and_44_out, and_45_out, and_46_out, and_47_out, and_48_out, and_49_out,
       and_50_out, and_51_out, and_52_out, and_53_out, and_54_out, and_55_out, and_56_out, and_57_out,
       and_58_out, and_59_out, and_60_out, and_61_out, and_62_out, and_63_out, and_64_out, and_65_out,
       and_66_out, and_67_out, and_68_out, and_69_out, and_70_out, and_71_out, and_72_out, and_73_out,
       and_74_out, and_75_out, and_76_out, and_77_out, and_78_out, and_79_out, and_80_out, nor_1_out,
       nor_2_out, nor_3_out, nor_4_out, nor_5_out, nor_6_out, nor_7_out, nor_8_out, nor_9_out, nor_10_out,
       nor_11_out, nor_12_out, nor_13_out, nor_14_out, nor_15_out, nor_16_out, nor_17_out, nor_18_out,
       nor_19_out, nor_20_out, nor_21_out, nor_22_out, nor_23_out, nor_24_out, nor_25_out, nor_26_out,
       nor_27_out, nor_28_out, nor_29_out, nor_30_out, nor_31_out, nor_32_out, nor_34_out, nor_36_out,
       nor_38_out, nor_40_out, nor_42_out, nor_44_out, nor_46_out, nor_48_out, nor_50_out, nor_52_out,
       nor_54_out, nor_56_out, nor_58_out, nor_60_out, nor_62_out, nor_64_out, not_1_out, not_2_out,
       not_3_out, not_4_out, not_5_out, not_6_out, not_7_out, not_8_out, not_9_out, not_10_out, not_11_out,
       not_12_out, not_13_out, not_14_out, not_15_out, not_16_out;

  not not_1 (not_1_out, and_1_out);
  and and_1 (and_1_out, CK, E);
  not not_2 (not_2_out, and_2_out);
  and and_2 (and_2_out, CK, E);
  not not_3 (not_3_out, and_3_out);
  and and_3 (and_3_out, CK, E);
  not not_4 (not_4_out, and_4_out);
  and and_4 (and_4_out, CK, E);
  not not_5 (not_5_out, and_5_out);
  and and_5 (and_5_out, CK, E);
  not not_6 (not_6_out, and_6_out);
  and and_6 (and_6_out, CK, E);
  and and_7 (and_7_out, ~Data[6], not_7_out);  // AND_Gate
  and and_8 (and_8_out, not_7_out, Data[6]);
  not not_7 (not_7_out, and_9_out);
  and and_9 (and_9_out, CK, E);
  and and_10 (and_10_out, ~Data[7], not_8_out);  // AND_Gate
  and and_11 (and_11_out, not_8_out, Data[7]);
  not not_8 (not_8_out, and_12_out);
  and and_12 (and_12_out, CK, E);
  and and_13 (and_13_out, ~Data[8], not_9_out);  // AND_Gate
  not not_9 (not_9_out, and_15_out);
  and and_14 (and_14_out, not_9_out, Data[8]);
  and and_15 (and_15_out, CK, E);
  and and_16 (and_16_out, ~Data[9], not_10_out);  // AND_Gate
  not not_10 (not_10_out, and_18_out);
  and and_17 (and_17_out, not_10_out, Data[9]);
  and and_18 (and_18_out, CK, E);
  and and_19 (and_19_out, ~Data[10], not_11_out);  // AND_Gate
  and and_20 (and_20_out, not_11_out, Data[10]);
  not not_11 (not_11_out, and_21_out);
  and and_21 (and_21_out, CK, E);
  and and_22 (and_22_out, ~Data[11], not_12_out);  // AND_Gate
  not not_12 (not_12_out, and_24_out);
  and and_23 (and_23_out, not_12_out, Data[11]);
  and and_24 (and_24_out, CK, E);
  and and_25 (and_25_out, ~Data[12], not_13_out);  // AND_Gate
  and and_26 (and_26_out, not_13_out, Data[12]);
  not not_13 (not_13_out, and_27_out);
  and and_27 (and_27_out, CK, E);
  and and_28 (and_28_out, ~Data[13], not_14_out);  // AND_Gate
  not not_14 (not_14_out, and_30_out);
  and and_29 (and_29_out, not_14_out, Data[13]);
  and and_30 (and_30_out, CK, E);
  and and_31 (and_31_out, ~Data[14], not_15_out);  // AND_Gate
  and and_32 (and_32_out, not_15_out, Data[14]);
  not not_15 (not_15_out, and_33_out);
  and and_33 (and_33_out, CK, E);
  and and_34 (and_34_out, ~Data[15], not_16_out);  // AND_Gate
  not not_16 (not_16_out, and_36_out);
  and and_35 (and_35_out, not_16_out, Data[15]);
  and and_36 (and_36_out, CK, E);
  and and_37 (and_37_out, ~Data[0], not_1_out);  // AND_Gate
  nor nor_1 (nor_1_out, R, and_37_out, nor_2_out);
  nor nor_2 (nor_2_out, nor_1_out, and_38_out, S);
  and and_38 (and_38_out, not_1_out, Data[0]);
  and and_39 (and_39_out, ~Data[1], not_2_out);  // AND_Gate
  nor nor_3 (nor_3_out, R, and_39_out, nor_4_out);
  nor nor_4 (nor_4_out, nor_3_out, and_40_out, S);
  and and_40 (and_40_out, not_2_out, Data[1]);
  nor nor_5 (nor_5_out, R, and_41_out, nor_6_out);
  and and_41 (and_41_out, ~Data[2], not_3_out);  // AND_Gate
  and and_42 (and_42_out, not_3_out, Data[2]);
  nor nor_6 (nor_6_out, nor_5_out, and_42_out, S);
  and and_43 (and_43_out, ~Data[3], not_4_out);  // AND_Gate
  nor nor_7 (nor_7_out, R, and_43_out, nor_8_out);
  nor nor_8 (nor_8_out, nor_7_out, and_44_out, S);
  and and_44 (and_44_out, not_4_out, Data[3]);
  nor nor_9 (nor_9_out, R, and_45_out, nor_10_out);
  and and_45 (and_45_out, ~Data[4], not_5_out);  // AND_Gate
  and and_46 (and_46_out, not_5_out, Data[4]);
  nor nor_10 (nor_10_out, nor_9_out, and_46_out, S);
  and and_47 (and_47_out, ~Data[5], not_6_out);  // AND_Gate
  nor nor_11 (nor_11_out, R, and_47_out, nor_12_out);
  and and_48 (and_48_out, not_6_out, Data[5]);
  nor nor_12 (nor_12_out, nor_11_out, and_48_out, S);
  nor nor_13 (nor_13_out, R, and_7_out, nor_14_out);
  nor nor_14 (nor_14_out, nor_13_out, and_8_out, S);
  nor nor_15 (nor_15_out, R, and_10_out, nor_16_out);
  nor nor_16 (nor_16_out, nor_15_out, and_11_out, S);
  nor nor_17 (nor_17_out, R, and_13_out, nor_18_out);
  nor nor_18 (nor_18_out, nor_17_out, and_14_out, S);
  nor nor_19 (nor_19_out, R, and_16_out, nor_20_out);
  nor nor_20 (nor_20_out, nor_19_out, and_17_out, S);
  nor nor_21 (nor_21_out, R, and_19_out, nor_22_out);
  nor nor_22 (nor_22_out, nor_21_out, and_20_out, S);
  nor nor_23 (nor_23_out, R, and_22_out, nor_24_out);
  nor nor_24 (nor_24_out, nor_23_out, and_23_out, S);
  nor nor_25 (nor_25_out, R, and_25_out, nor_26_out);
  nor nor_26 (nor_26_out, nor_25_out, and_26_out, S);
  nor nor_27 (nor_27_out, R, and_28_out, nor_28_out);
  nor nor_28 (nor_28_out, nor_27_out, and_29_out, S);
  nor nor_29 (nor_29_out, R, and_31_out, nor_30_out);
  nor nor_30 (nor_30_out, nor_29_out, and_32_out, S);
  nor nor_31 (nor_31_out, R, and_34_out, nor_32_out);
  nor nor_32 (nor_32_out, nor_31_out, and_35_out, S);
  and and_49 (and_49_out, ~nor_1_out, and_1_out);  // AND_Gate
  and and_50 (and_50_out, and_1_out, nor_1_out);
  and and_51 (and_51_out, ~nor_3_out, and_2_out);  // AND_Gate
  and and_52 (and_52_out, and_2_out, nor_3_out);
  and and_53 (and_53_out, ~nor_5_out, and_3_out);  // AND_Gate
  and and_54 (and_54_out, and_3_out, nor_5_out);
  and and_55 (and_55_out, ~nor_7_out, and_4_out);  // AND_Gate
  and and_56 (and_56_out, and_4_out, nor_7_out);
  and and_57 (and_57_out, ~nor_9_out, and_5_out);  // AND_Gate
  and and_58 (and_58_out, and_5_out, nor_9_out);
  and and_59 (and_59_out, ~nor_11_out, and_6_out);  // AND_Gate
  and and_60 (and_60_out, and_6_out, nor_11_out);
  and and_61 (and_61_out, ~nor_13_out, and_9_out);  // AND_Gate
  and and_62 (and_62_out, and_9_out, nor_13_out);
  and and_63 (and_63_out, ~nor_15_out, and_12_out);  // AND_Gate
  and and_64 (and_64_out, and_12_out, nor_15_out);
  and and_65 (and_65_out, ~nor_17_out, and_15_out);  // AND_Gate
  and and_66 (and_66_out, and_15_out, nor_17_out);
  and and_67 (and_67_out, ~nor_19_out, and_18_out);  // AND_Gate
  and and_68 (and_68_out, and_18_out, nor_19_out);
  and and_69 (and_69_out, ~nor_21_out, and_21_out);  // AND_Gate
  and and_70 (and_70_out, and_21_out, nor_21_out);
  and and_71 (and_71_out, ~nor_23_out, and_24_out);  // AND_Gate
  and and_72 (and_72_out, and_24_out, nor_23_out);
  and and_73 (and_73_out, ~nor_25_out, and_27_out);  // AND_Gate
  and and_74 (and_74_out, and_27_out, nor_25_out);
  and and_75 (and_75_out, ~nor_27_out, and_30_out);  // AND_Gate
  and and_76 (and_76_out, and_30_out, nor_27_out);
  and and_77 (and_77_out, ~nor_29_out, and_33_out);  // AND_Gate
  and and_78 (and_78_out, and_33_out, nor_29_out);
  and and_79 (and_79_out, ~nor_31_out, and_36_out);  // AND_Gate
  and and_80 (and_80_out, and_36_out, nor_31_out);
  nor nor_33 (Out[0], R, and_49_out, nor_34_out);
  nor nor_34 (nor_34_out, Out[0], and_50_out, S);
  nor nor_35 (Out[1], R, and_51_out, nor_36_out);
  nor nor_36 (nor_36_out, Out[1], and_52_out, S);
  nor nor_37 (Out[2], R, and_53_out, nor_38_out);
  nor nor_38 (nor_38_out, Out[2], and_54_out, S);
  nor nor_39 (Out[3], R, and_55_out, nor_40_out);
  nor nor_40 (nor_40_out, Out[3], and_56_out, S);
  nor nor_41 (Out[4], R, and_57_out, nor_42_out);
  nor nor_42 (nor_42_out, Out[4], and_58_out, S);
  nor nor_43 (Out[5], R, and_59_out, nor_44_out);
  nor nor_44 (nor_44_out, Out[5], and_60_out, S);
  nor nor_45 (Out[6], R, and_61_out, nor_46_out);
  nor nor_46 (nor_46_out, Out[6], and_62_out, S);
  nor nor_47 (Out[7], R, and_63_out, nor_48_out);
  nor nor_48 (nor_48_out, Out[7], and_64_out, S);
  nor nor_49 (Out[8], R, and_65_out, nor_50_out);
  nor nor_50 (nor_50_out, Out[8], and_66_out, S);
  nor nor_51 (Out[9], R, and_67_out, nor_52_out);
  nor nor_52 (nor_52_out, Out[9], and_68_out, S);
  nor nor_53 (Out[10], R, and_69_out, nor_54_out);
  nor nor_54 (nor_54_out, Out[10], and_70_out, S);
  nor nor_55 (Out[11], R, and_71_out, nor_56_out);
  nor nor_56 (nor_56_out, Out[11], and_72_out, S);
  nor nor_57 (Out[12], R, and_73_out, nor_58_out);
  nor nor_58 (nor_58_out, Out[12], and_74_out, S);
  nor nor_59 (Out[13], R, and_75_out, nor_60_out);
  nor nor_60 (nor_60_out, Out[13], and_76_out, S);
  nor nor_61 (Out[14], R, and_77_out, nor_62_out);
  nor nor_62 (nor_62_out, Out[14], and_78_out, S);
  nor nor_63 (Out[15], R, and_79_out, nor_64_out);
  nor nor_64 (nor_64_out, Out[15], and_80_out, S);

  // Notes on the sheet:
  //   E: pull=down
  //   Data: pull=down
  //   R: pull=down
  //   S: pull=down
  //   CK: pull=down
  //   Out: pull=down
endmodule

module Multi_A_Men_16 (
  input  [3:0] in_1,
  output [15:0] out_2
);

  and and_1 (out_2[0], ~in_1[3], ~in_1[2], ~in_1[1], ~in_1[0]);  // AND_Gate
  and and_2 (out_2[1], ~in_1[3], ~in_1[2], ~in_1[1], in_1[0]);  // AND_Gate
  and and_3 (out_2[2], ~in_1[3], ~in_1[2], in_1[1], ~in_1[0]);  // AND_Gate
  and and_4 (out_2[3], ~in_1[3], ~in_1[2], in_1[1], in_1[0]);  // AND_Gate
  and and_5 (out_2[4], ~in_1[3], in_1[2], ~in_1[1], ~in_1[0]);  // AND_Gate
  and and_6 (out_2[5], ~in_1[3], in_1[2], ~in_1[1], in_1[0]);  // AND_Gate
  and and_7 (out_2[6], ~in_1[3], in_1[2], in_1[1], ~in_1[0]);  // AND_Gate
  and and_8 (out_2[7], ~in_1[3], in_1[2], in_1[1], in_1[0]);  // AND_Gate
  and and_9 (out_2[8], in_1[3], ~in_1[2], ~in_1[1], ~in_1[0]);  // AND_Gate
  and and_10 (out_2[9], in_1[3], ~in_1[2], ~in_1[1], in_1[0]);  // AND_Gate
  and and_11 (out_2[10], in_1[3], ~in_1[2], in_1[1], ~in_1[0]);  // AND_Gate
  and and_12 (out_2[11], in_1[3], ~in_1[2], in_1[1], in_1[0]);  // AND_Gate
  and and_13 (out_2[12], in_1[3], in_1[2], ~in_1[1], ~in_1[0]);  // AND_Gate
  and and_14 (out_2[13], in_1[3], in_1[2], ~in_1[1], in_1[0]);  // AND_Gate
  and and_15 (out_2[14], in_1[3], in_1[2], in_1[1], ~in_1[0]);  // AND_Gate
  and and_16 (out_2[15], in_1[3], in_1[2], in_1[1], in_1[0]);

  // Notes on the sheet:
  //   out_2: pull=down
  //   in_1: pull=down
endmodule

module Select_16b (
  input  E,
  input  [15:0] In,
  output [15:0] Out
);

  and and_1 (Out[0], E, In[0]);
  and and_2 (Out[1], E, In[1]);
  and and_3 (Out[2], E, In[2]);
  and and_4 (Out[3], E, In[3]);
  and and_5 (Out[4], E, In[4]);
  and and_6 (Out[5], E, In[5]);
  and and_7 (Out[6], E, In[6]);
  and and_8 (Out[7], E, In[7]);
  and and_9 (Out[8], In[8], E);
  and and_10 (Out[9], In[9], E);
  and and_11 (Out[10], In[10], E);
  and and_12 (Out[11], In[11], E);
  and and_13 (Out[12], In[12], E);
  and and_14 (Out[13], In[13], E);
  and and_15 (Out[14], In[14], E);
  and and_16 (Out[15], In[15], E);

  // Notes on the sheet:
  //   E: pull=down
  //   In: pull=down
  //   Out: pull=down
endmodule

module Multi_B_Men_16b (
  input  [3:0] Adress,
  input  [15:0] _15,
  input  [15:0] _14,
  input  [15:0] _13,
  input  [15:0] _12,
  input  [15:0] _11,
  input  [15:0] _10,
  input  [15:0] _9,
  input  [15:0] _8,
  input  [15:0] _7,
  input  [15:0] _6,
  input  [15:0] _5,
  input  [15:0] _4,
  input  [15:0] _3,
  input  [15:0] _2,
  input  [15:0] _1,
  input  [15:0] _0,
  output [15:0] Out
);

  wire [15:0] controlled_buffer_1_out, controlled_buffer_2_out, controlled_buffer_3_out,
       controlled_buffer_4_out, controlled_buffer_5_out, controlled_buffer_6_out, controlled_buffer_7_out,
       controlled_buffer_8_out, controlled_buffer_9_out, controlled_buffer_10_out, controlled_buffer_11_out,
       controlled_buffer_12_out, controlled_buffer_13_out, controlled_buffer_14_out,
       controlled_buffer_15_out, controlled_buffer_16_out, multi_a_men_16_1_out_2;

  Multi_A_Men_16 multi_a_men_16_1 (.in_1(Adress), .out_2(multi_a_men_16_1_out_2));
  assign controlled_buffer_1_out = multi_a_men_16_1_out_2[15] ? _15 : 16'bz;  // Controlled_Buffer controlled_buffer_1
  assign controlled_buffer_2_out = multi_a_men_16_1_out_2[14] ? _14 : 16'bz;  // Controlled_Buffer controlled_buffer_2
  assign controlled_buffer_3_out = multi_a_men_16_1_out_2[13] ? _13 : 16'bz;  // Controlled_Buffer controlled_buffer_3
  assign controlled_buffer_4_out = multi_a_men_16_1_out_2[12] ? _12 : 16'bz;  // Controlled_Buffer controlled_buffer_4
  assign controlled_buffer_5_out = multi_a_men_16_1_out_2[11] ? _11 : 16'bz;  // Controlled_Buffer controlled_buffer_5
  assign controlled_buffer_6_out = multi_a_men_16_1_out_2[10] ? _10 : 16'bz;  // Controlled_Buffer controlled_buffer_6
  assign controlled_buffer_7_out = multi_a_men_16_1_out_2[9] ? _9 : 16'bz;  // Controlled_Buffer controlled_buffer_7
  assign controlled_buffer_8_out = multi_a_men_16_1_out_2[8] ? _8 : 16'bz;  // Controlled_Buffer controlled_buffer_8
  assign controlled_buffer_9_out = multi_a_men_16_1_out_2[7] ? _7 : 16'bz;  // Controlled_Buffer controlled_buffer_9
  assign controlled_buffer_10_out = multi_a_men_16_1_out_2[6] ? _6 : 16'bz;  // Controlled_Buffer controlled_buffer_10
  assign controlled_buffer_11_out = multi_a_men_16_1_out_2[5] ? _5 : 16'bz;  // Controlled_Buffer controlled_buffer_11
  assign controlled_buffer_12_out = multi_a_men_16_1_out_2[4] ? _4 : 16'bz;  // Controlled_Buffer controlled_buffer_12
  assign controlled_buffer_13_out = multi_a_men_16_1_out_2[3] ? _3 : 16'bz;  // Controlled_Buffer controlled_buffer_13
  assign controlled_buffer_14_out = multi_a_men_16_1_out_2[2] ? _2 : 16'bz;  // Controlled_Buffer controlled_buffer_14
  assign controlled_buffer_15_out = multi_a_men_16_1_out_2[1] ? _1 : 16'bz;  // Controlled_Buffer controlled_buffer_15
  assign controlled_buffer_16_out = multi_a_men_16_1_out_2[0] ? _0 : 16'bz;  // Controlled_Buffer controlled_buffer_16
  OR_Men_16b or_men_16b_1 (
    ._15(controlled_buffer_1_out), ._14(controlled_buffer_2_out), ._13(controlled_buffer_3_out),
    ._12(controlled_buffer_4_out), ._11(controlled_buffer_5_out), ._10(controlled_buffer_6_out),
    ._9(controlled_buffer_7_out), ._8(controlled_buffer_8_out), ._7(controlled_buffer_9_out),
    ._6(controlled_buffer_10_out), ._5(controlled_buffer_11_out), ._4(controlled_buffer_12_out),
    ._3(controlled_buffer_13_out), ._2(controlled_buffer_14_out), ._1(controlled_buffer_15_out),
    ._0(controlled_buffer_16_out), .out_17(Out));

  // Notes on the sheet:
  //   _0: pull=down
  //   _3: pull=down
  //   _4: pull=down
  //   _8: pull=down
  //   Adress: pull=down
  //   Out: pull=down
  //   _2: pull=down
  //   _11: pull=down
  //   _13: pull=down
  //   _12: pull=down
  //   _9: pull=down
  //   _14: pull=down
  //   _5: pull=down
  //   _10: pull=down
  //   _7: pull=down
  //   _1: pull=down
  //   _6: pull=down
  //   _15: pull=down
endmodule

module OR_Men_16b (
  input  [15:0] _15,
  input  [15:0] _14,
  input  [15:0] _13,
  input  [15:0] _12,
  input  [15:0] _11,
  input  [15:0] _10,
  input  [15:0] _9,
  input  [15:0] _8,
  input  [15:0] _7,
  input  [15:0] _6,
  input  [15:0] _5,
  input  [15:0] _4,
  input  [15:0] _3,
  input  [15:0] _2,
  input  [15:0] _1,
  input  [15:0] _0,
  output [15:0] out_17
);

  assign out_17 = _15 | _14 | _13 | _12 | _11 | _10 | _9 | _8 | _7 | _6 | _5 | _4 | _3 | _2 | _1 | _0;  // OR_Gate or_1, 16 bits wide

  // Notes on the sheet:
  //   _9: pull=down
  //   _5: pull=down
  //   out_17: pull=down
  //   _3: pull=down
  //   _1: pull=down
  //   _7: pull=down
  //   _2: pull=down
  //   _15: pull=down
  //   _14: pull=down
  //   _4: pull=down
  //   _6: pull=down
  //   _13: pull=down
  //   _0: pull=down
  //   _8: pull=down
  //   _12: pull=down
  //   _10: pull=down
  //   _11: pull=down
endmodule

module Contador (
  input  Start,
  input  [7:0] in_2,
  input  in_3,
  input  [15:0] in_4,
  input  [2:0] in_5
);

  wire and_1_out, button_1_out, button_2_out, clock_1_out, R_out, S_out;
  wire [2:0] or_1_out;
  wire [7:0] Add, ctrl_display_d_1_out_2, ctrl_display_u_1_out_2, somador_1_out;
  wire [15:0] memoria_8x16b_1_out_1;

  Clock clock_1 (.out(clock_1_out));
  assign or_1_out = in_5 | Add[2:0];  // OR_Gate or_1, 3 bits wide
  and and_1 (and_1_out, clock_1_out, Start);
  Button R (.out(R_out));
  Button S (.out(S_out));
  Button button_1 (.out(button_1_out));
  Button button_2 (.out(button_2_out));
  Memoria_8x16b memoria_8x16b_1 (
    .S(S_out), .R(R_out), .Cl(clock_1_out), .W(in_3), .Data(in_4), .Andress(or_1_out), .Rs(or_1_out),
    .Out_1(memoria_8x16b_1_out_1));  // open: Rt, Out_2
  Palavra_8b palavra_8b_1 (
    .Data(somador_1_out), .Out(Add), .CK(and_1_out), .E(and_1_out), .R(button_2_out), .S(button_1_out));
  Somador somador_1 (.A(Add), .B(in_2), .Out(somador_1_out));
  DotMatrix #(.inputtype("row"), .matrixcols(4), .matrixrows(4)) dotmatrix_1 (
    .row0(memoria_8x16b_1_out_1[3:0]), .row1(memoria_8x16b_1_out_1[7:4]), .row2(memoria_8x16b_1_out_1[11:8]),
    .row3(memoria_8x16b_1_out_1[15:12]));
  Ctrl_Display_U ctrl_display_u_1 (.in_1(somador_1_out[3:0]), .out_2(ctrl_display_u_1_out_2));
  Ctrl_Display_D ctrl_display_d_1 (.in_1(somador_1_out[3:0]), .out_2(ctrl_display_d_1_out_2));
  _7_Segment_Display u_7_segment_display_1 (
    .g(ctrl_display_u_1_out_2[3]), .f(ctrl_display_u_1_out_2[2]), .a(ctrl_display_u_1_out_2[1]),
    .b(ctrl_display_u_1_out_2[0]), .e(ctrl_display_u_1_out_2[7]), .d(ctrl_display_u_1_out_2[6]),
    .c(ctrl_display_u_1_out_2[5]), .dp(ctrl_display_u_1_out_2[4]));
  _7_Segment_Display u_7_segment_display_2 (
    .g(ctrl_display_d_1_out_2[3]), .f(ctrl_display_d_1_out_2[2]), .a(ctrl_display_d_1_out_2[1]),
    .b(ctrl_display_d_1_out_2[0]), .e(ctrl_display_d_1_out_2[7]), .d(ctrl_display_d_1_out_2[6]),
    .c(ctrl_display_d_1_out_2[5]), .dp(ctrl_display_d_1_out_2[4]));

  // Notes on the sheet:
  //   in_2: pull=down
  //   in_4: pull=down
endmodule

module Ctrl_Display_U (
  input  [3:0] in_1,
  output [7:0] out_2
);

  wire and_1_out, and_2_out, and_3_out, and_4_out, and_5_out, and_6_out, and_7_out, and_8_out, and_9_out,
       and_10_out, and_11_out, and_12_out, and_13_out, and_14_out, and_15_out, and_16_out, and_17_out,
       and_18_out, and_19_out, and_20_out, and_21_out, and_22_out, and_23_out, and_24_out, and_25_out,
       and_26_out, and_27_out, and_28_out, and_29_out, and_30_out, and_31_out;

  and and_1 (and_1_out, ~in_1[1], ~in_1[0]);  // AND_Gate
  and and_2 (and_2_out, in_1[3], ~in_1[1]);  // AND_Gate
  and and_3 (and_3_out, in_1[3], ~in_1[0]);  // AND_Gate
  and and_4 (and_4_out, ~in_1[3], in_1[1], in_1[0]);  // AND_Gate
  and and_5 (and_5_out, ~in_1[2], ~in_1[0]);  // AND_Gate
  and and_6 (and_6_out, ~in_1[3], in_1[1]);  // AND_Gate
  and and_7 (and_7_out, in_1[2], in_1[0]);
  and and_8 (and_8_out, in_1[3], ~in_1[1]);  // AND_Gate
  and and_9 (and_9_out, ~in_1[3], ~in_1[1], ~in_1[0]);  // AND_Gate
  and and_10 (and_10_out, ~in_1[3], in_1[2], ~in_1[1]);  // AND_Gate
  and and_11 (and_11_out, ~in_1[3], in_1[2], ~in_1[0]);  // AND_Gate
  and and_12 (and_12_out, in_1[3], ~in_1[2], ~in_1[1]);  // AND_Gate
  and and_13 (and_13_out, in_1[3], ~in_1[2], ~in_1[0]);  // AND_Gate
  and and_14 (and_14_out, in_1[3], in_1[2], in_1[1]);
  and and_15 (and_15_out, in_1[2], ~in_1[1]);  // AND_Gate
  and and_16 (and_16_out, in_1[2], ~in_1[0]);  // AND_Gate
  and and_17 (and_17_out, in_1[3], ~in_1[1]);  // AND_Gate
  and and_18 (and_18_out, in_1[3], in_1[2]);
  and and_19 (and_19_out, ~in_1[3], ~in_1[2], in_1[1]);  // AND_Gate
  and and_20 (and_20_out, ~in_1[3], ~in_1[1]);  // AND_Gate
  and and_21 (and_21_out, in_1[2], in_1[1]);
  and and_22 (and_22_out, in_1[3], ~in_1[2]);  // AND_Gate
  and and_23 (and_23_out, ~in_1[2], ~in_1[0]);  // AND_Gate
  and and_24 (and_24_out, in_1[3], ~in_1[1]);  // AND_Gate
  and and_25 (and_25_out, ~in_1[3], ~in_1[2], in_1[1]);  // AND_Gate
  and and_26 (and_26_out, ~in_1[3], in_1[1], ~in_1[0]);  // AND_Gate
  and and_27 (and_27_out, in_1[2], ~in_1[1], in_1[0]);  // AND_Gate
  and and_28 (and_28_out, in_1[3], in_1[2], in_1[0]);
  and and_29 (and_29_out, ~in_1[2], ~in_1[0]);  // AND_Gate
  and and_30 (and_30_out, ~in_1[3], in_1[1], ~in_1[0]);  // AND_Gate
  and and_31 (and_31_out, in_1[3], ~in_1[1], ~in_1[0]);  // AND_Gate
  or or_1 (out_2[0], ~in_1[2], and_1_out, and_2_out, and_3_out, and_4_out);  // OR_Gate
  or or_2 (out_2[1], and_5_out, and_6_out, and_7_out, and_8_out);
  or or_3 (out_2[3], and_15_out, and_16_out, and_17_out, and_18_out, and_19_out);
  or or_4 (out_2[5], in_1[0], and_20_out, and_21_out, and_22_out);
  or or_5 (out_2[7], and_29_out, and_30_out, and_31_out);
  not not_1 (out_2[4], 1'b1);
  or or_6 (out_2[2], and_9_out, and_10_out, and_11_out, and_12_out, and_13_out, and_14_out);
  or or_7 (out_2[6], and_23_out, and_24_out, and_25_out, and_26_out, and_27_out, and_28_out);

  // Notes on the sheet:
  //   out_2: pull=down
  //   in_1: pull=down
endmodule

module Ctrl_Display_D (
  input  [3:0] in_1,
  output [7:0] out_2
);

  wire and_1_out;

  and and_1 (and_1_out, ~in_1[2], ~in_1[1]);  // AND_Gate
  or or_1 (out_2[7], and_1_out, ~in_1[3]);  // OR_Gate
  not not_1 (out_2[3], 1'b1);
  not not_2 (out_2[4], 1'b1);

  assign {out_2[6:5], out_2[2:0]} = {out_2[7], 1'b1, {2{out_2[7]}}, 1'b1};

  // Notes on the sheet:
  //   in_1: pull=down
  //   out_2: pull=down
endmodule

module Memoria_8x16b (
  input  S,
  input  R,
  input  Cl,
  input  W,
  input  [15:0] Data,
  input  [2:0] Andress,
  input  [2:0] Rs,
  input  [2:0] Rt,
  output [15:0] Out_1,
  output [15:0] Out_2
);

  wire and_1_out, multi_a_men_8b_1__0, multi_a_men_8b_1__1, multi_a_men_8b_1__2, multi_a_men_8b_1__3,
       multi_a_men_8b_1__4, multi_a_men_8b_1__5, multi_a_men_8b_1__6, multi_a_men_8b_1__7,
       multi_a_men_8b_2__0, multi_a_men_8b_2__1, multi_a_men_8b_2__2, multi_a_men_8b_2__3,
       multi_a_men_8b_2__4, multi_a_men_8b_2__5, multi_a_men_8b_2__6, multi_a_men_8b_2__7,
       multi_a_men_8b_3__0, multi_a_men_8b_3__1, multi_a_men_8b_3__2, multi_a_men_8b_3__3,
       multi_a_men_8b_3__4, multi_a_men_8b_3__5, multi_a_men_8b_3__6, multi_a_men_8b_3__7;
  wire [15:0] _0, _1, _2, _3, _4, _5, _6, _7, select_16b_1_out, select_16b_2_out, select_16b_3_out,
       select_16b_4_out, select_16b_5_out, select_16b_6_out, select_16b_7_out, select_16b_8_out,
       select_16b_9_out, select_16b_10_out, select_16b_11_out, select_16b_12_out, select_16b_13_out,
       select_16b_14_out, select_16b_15_out, select_16b_16_out;

  and and_1 (and_1_out, Cl, W);
  Multi_A_Men_8b multi_a_men_8b_1 (
    .in_1(Andress), ._0(multi_a_men_8b_1__0), ._1(multi_a_men_8b_1__1), ._2(multi_a_men_8b_1__2),
    ._3(multi_a_men_8b_1__3), ._4(multi_a_men_8b_1__4), ._5(multi_a_men_8b_1__5), ._6(multi_a_men_8b_1__6),
    ._7(multi_a_men_8b_1__7));
  Multi_A_Men_8b multi_a_men_8b_2 (
    .in_1(Rs), ._0(multi_a_men_8b_2__0), ._1(multi_a_men_8b_2__1), ._2(multi_a_men_8b_2__2),
    ._3(multi_a_men_8b_2__3), ._4(multi_a_men_8b_2__4), ._5(multi_a_men_8b_2__5), ._6(multi_a_men_8b_2__6),
    ._7(multi_a_men_8b_2__7));
  Multi_A_Men_8b multi_a_men_8b_3 (
    .in_1(Rt), ._0(multi_a_men_8b_3__0), ._1(multi_a_men_8b_3__1), ._2(multi_a_men_8b_3__2),
    ._3(multi_a_men_8b_3__3), ._4(multi_a_men_8b_3__4), ._5(multi_a_men_8b_3__5), ._6(multi_a_men_8b_3__6),
    ._7(multi_a_men_8b_3__7));
  Palavra_16b palavra_16b_1 (.Data(Data), .CK(and_1_out), .E(multi_a_men_8b_1__0), .R(R), .S(S), .Out(_0));
  Select_16b select_16b_1 (.In(_0), .Out(select_16b_1_out), .E(multi_a_men_8b_2__0));
  Select_16b select_16b_2 (.In(_1), .Out(select_16b_2_out), .E(multi_a_men_8b_2__1));
  Select_16b select_16b_3 (.In(_0), .Out(select_16b_3_out), .E(multi_a_men_8b_3__0));
  Select_16b select_16b_4 (.In(_1), .Out(select_16b_4_out), .E(multi_a_men_8b_3__1));
  Select_16b select_16b_5 (.In(_2), .Out(select_16b_5_out), .E(multi_a_men_8b_2__2));
  Select_16b select_16b_6 (.In(_3), .Out(select_16b_6_out), .E(multi_a_men_8b_2__3));
  Select_16b select_16b_7 (.In(_2), .Out(select_16b_7_out), .E(multi_a_men_8b_3__2));
  Select_16b select_16b_8 (.In(_3), .Out(select_16b_8_out), .E(multi_a_men_8b_3__3));
  Palavra_16b palavra_16b_2 (.Data(Data), .CK(and_1_out), .E(multi_a_men_8b_1__1), .R(R), .S(S), .Out(_1));
  Select_16b select_16b_9 (.In(_4), .Out(select_16b_9_out), .E(multi_a_men_8b_2__4));
  Select_16b select_16b_10 (.In(_5), .Out(select_16b_10_out), .E(multi_a_men_8b_2__5));
  Select_16b select_16b_11 (.In(_4), .Out(select_16b_11_out), .E(multi_a_men_8b_3__4));
  Select_16b select_16b_12 (.In(_5), .Out(select_16b_12_out), .E(multi_a_men_8b_3__5));
  Palavra_16b palavra_16b_3 (.Data(Data), .CK(and_1_out), .E(multi_a_men_8b_1__2), .R(R), .S(S), .Out(_2));
  Select_16b select_16b_13 (.In(_6), .Out(select_16b_13_out), .E(multi_a_men_8b_2__6));
  Select_16b select_16b_14 (.In(_7), .Out(select_16b_14_out), .E(multi_a_men_8b_2__7));
  Select_16b select_16b_15 (.In(_6), .Out(select_16b_15_out), .E(multi_a_men_8b_3__6));
  Select_16b select_16b_16 (.In(_7), .Out(select_16b_16_out), .E(multi_a_men_8b_3__7));
  Palavra_16b palavra_16b_4 (.Data(Data), .CK(and_1_out), .E(multi_a_men_8b_1__3), .R(R), .S(S), .Out(_3));
  Palavra_16b palavra_16b_5 (.Data(Data), .CK(and_1_out), .E(multi_a_men_8b_1__4), .R(R), .S(S), .Out(_4));
  assign Out_1 = select_16b_1_out | select_16b_2_out | select_16b_5_out | select_16b_6_out | select_16b_9_out | select_16b_10_out | select_16b_13_out | select_16b_14_out;  // OR_Gate or_1, 16 bits wide
  assign Out_2 = select_16b_3_out | select_16b_4_out | select_16b_7_out | select_16b_8_out | select_16b_11_out | select_16b_12_out | select_16b_15_out | select_16b_16_out;  // OR_Gate or_2, 16 bits wide
  Palavra_16b palavra_16b_6 (.Data(Data), .CK(and_1_out), .E(multi_a_men_8b_1__5), .R(R), .S(S), .Out(_5));
  Palavra_16b palavra_16b_7 (.Data(Data), .CK(and_1_out), .E(multi_a_men_8b_1__6), .R(R), .S(S), .Out(_6));
  Palavra_16b palavra_16b_8 (.Data(Data), .CK(and_1_out), .E(multi_a_men_8b_1__7), .R(R), .S(S), .Out(_7));

  // Notes on the sheet:
  //   Rs: pull=down
  //   Data: pull=down
  //   Out_2: pull=down
  //   Cl: pull=down
  //   S: pull=down
  //   Andress: pull=down
  //   W: pull=down
  //   Rt: pull=down
  //   R: pull=down
  //   Out_1: pull=down
endmodule

module Add_16b (
  input  [15:0] A,
  input  [15:0] B,
  output [15:0] out_3
);

  wire and_1_out, and_2_out, and_3_out, and_4_out, and_5_out, and_6_out, and_7_out, and_8_out, and_9_out,
       and_10_out, and_11_out, and_12_out, and_13_out, and_14_out, and_15_out, and_16_out, and_17_out,
       and_18_out, and_19_out, and_20_out, and_21_out, and_22_out, and_23_out, and_24_out, and_25_out,
       and_26_out, and_27_out, and_28_out, and_29_out, and_30_out, and_31_out, and_32_out, and_33_out,
       and_34_out, and_35_out, and_36_out, and_37_out, and_38_out, and_39_out, and_40_out, and_41_out,
       and_42_out, and_43_out, and_44_out, and_45_out, and_46_out, and_47_out, and_48_out, and_49_out,
       and_50_out, and_51_out, and_52_out, and_53_out, and_54_out, and_55_out, and_56_out, and_57_out,
       and_58_out, and_59_out, and_60_out, and_61_out, and_62_out, and_63_out, and_64_out, and_65_out,
       and_66_out, and_67_out, and_68_out, and_69_out, and_70_out, and_71_out, and_72_out, and_73_out,
       and_74_out, and_75_out, and_76_out, and_77_out, and_78_out, and_79_out, and_80_out, and_81_out,
       and_82_out, and_83_out, and_84_out, and_85_out, and_86_out, and_87_out, and_88_out, and_89_out,
       and_90_out, and_91_out, and_92_out, and_93_out, and_94_out, and_95_out, and_96_out, and_97_out,
       and_98_out, and_99_out, and_100_out, and_101_out, and_102_out, and_103_out, and_104_out, and_105_out,
       and_106_out, and_107_out, and_108_out, and_109_out, and_110_out, and_111_out, and_112_out,
       button_1_out, or_1_out, or_3_out, or_5_out, or_7_out, or_9_out, or_11_out, or_13_out, or_15_out,
       or_17_out, or_19_out, or_21_out, or_23_out, or_25_out, or_27_out, or_29_out, or_31_out;

  Button button_1 (.out(button_1_out));
  and and_1 (and_1_out, A[0], B[0]);
  and and_2 (and_2_out, button_1_out, B[0]);
  and and_3 (and_3_out, button_1_out, A[0]);
  and and_4 (and_4_out, ~button_1_out, ~A[0], B[0]);  // AND_Gate
  and and_5 (and_5_out, ~button_1_out, A[0], ~B[0]);  // AND_Gate
  and and_6 (and_6_out, button_1_out, ~A[0], ~B[0]);  // AND_Gate
  and and_7 (and_7_out, button_1_out, A[0], B[0]);
  or or_1 (or_1_out, and_1_out, and_2_out, and_3_out);
  or or_2 (out_3[0], and_4_out, and_5_out, and_6_out, and_7_out);
  and and_8 (and_8_out, A[1], B[1]);
  and and_9 (and_9_out, or_1_out, B[1]);
  and and_10 (and_10_out, or_1_out, A[1]);
  and and_11 (and_11_out, ~or_1_out, ~A[1], B[1]);  // AND_Gate
  and and_12 (and_12_out, ~or_1_out, A[1], ~B[1]);  // AND_Gate
  and and_13 (and_13_out, or_1_out, ~A[1], ~B[1]);  // AND_Gate
  and and_14 (and_14_out, or_1_out, A[1], B[1]);
  or or_3 (or_3_out, and_8_out, and_9_out, and_10_out);
  or or_4 (out_3[1], and_11_out, and_12_out, and_13_out, and_14_out);
  and and_15 (and_15_out, A[2], B[2]);
  and and_16 (and_16_out, or_3_out, B[2]);
  and and_17 (and_17_out, or_3_out, A[2]);
  and and_18 (and_18_out, ~or_3_out, ~A[2], B[2]);  // AND_Gate
  and and_19 (and_19_out, ~or_3_out, A[2], ~B[2]);  // AND_Gate
  and and_20 (and_20_out, or_3_out, ~A[2], ~B[2]);  // AND_Gate
  and and_21 (and_21_out, or_3_out, A[2], B[2]);
  or or_5 (or_5_out, and_15_out, and_16_out, and_17_out);
  or or_6 (out_3[2], and_18_out, and_19_out, and_20_out, and_21_out);
  and and_22 (and_22_out, A[3], B[3]);
  and and_23 (and_23_out, or_5_out, B[3]);
  and and_24 (and_24_out, or_5_out, A[3]);
  and and_25 (and_25_out, ~or_5_out, ~A[3], B[3]);  // AND_Gate
  and and_26 (and_26_out, ~or_5_out, A[3], ~B[3]);  // AND_Gate
  and and_27 (and_27_out, or_5_out, ~A[3], ~B[3]);  // AND_Gate
  and and_28 (and_28_out, or_5_out, A[3], B[3]);
  or or_7 (or_7_out, and_22_out, and_23_out, and_24_out);
  or or_8 (out_3[3], and_25_out, and_26_out, and_27_out, and_28_out);
  and and_29 (and_29_out, A[4], B[4]);
  and and_30 (and_30_out, or_7_out, B[4]);
  and and_31 (and_31_out, or_7_out, A[4]);
  and and_32 (and_32_out, ~or_7_out, ~A[4], B[4]);  // AND_Gate
  and and_33 (and_33_out, ~or_7_out, A[4], ~B[4]);  // AND_Gate
  and and_34 (and_34_out, or_7_out, ~A[4], ~B[4]);  // AND_Gate
  and and_35 (and_35_out, or_7_out, A[4], B[4]);
  or or_9 (or_9_out, and_29_out, and_30_out, and_31_out);
  or or_10 (out_3[4], and_32_out, and_33_out, and_34_out, and_35_out);
  and and_36 (and_36_out, A[5], B[5]);
  and and_37 (and_37_out, or_9_out, B[5]);
  and and_38 (and_38_out, or_9_out, A[5]);
  and and_39 (and_39_out, ~or_9_out, ~A[5], B[5]);  // AND_Gate
  and and_40 (and_40_out, ~or_9_out, A[5], ~B[5]);  // AND_Gate
  and and_41 (and_41_out, or_9_out, ~A[5], ~B[5]);  // AND_Gate
  and and_42 (and_42_out, or_9_out, A[5], B[5]);
  or or_11 (or_11_out, and_36_out, and_37_out, and_38_out);
  or or_12 (out_3[5], and_39_out, and_40_out, and_41_out, and_42_out);
  and and_43 (and_43_out, A[6], B[6]);
  and and_44 (and_44_out, or_11_out, B[6]);
  and and_45 (and_45_out, or_11_out, A[6]);
  and and_46 (and_46_out, ~or_11_out, ~A[6], B[6]);  // AND_Gate
  and and_47 (and_47_out, ~or_11_out, A[6], ~B[6]);  // AND_Gate
  and and_48 (and_48_out, or_11_out, ~A[6], ~B[6]);  // AND_Gate
  and and_49 (and_49_out, or_11_out, A[6], B[6]);
  or or_13 (or_13_out, and_43_out, and_44_out, and_45_out);
  or or_14 (out_3[6], and_46_out, and_47_out, and_48_out, and_49_out);
  and and_50 (and_50_out, A[7], B[7]);
  and and_51 (and_51_out, or_13_out, B[7]);
  and and_52 (and_52_out, or_13_out, A[7]);
  and and_53 (and_53_out, ~or_13_out, ~A[7], B[7]);  // AND_Gate
  and and_54 (and_54_out, ~or_13_out, A[7], ~B[7]);  // AND_Gate
  and and_55 (and_55_out, or_13_out, ~A[7], ~B[7]);  // AND_Gate
  and and_56 (and_56_out, or_13_out, A[7], B[7]);
  or or_15 (or_15_out, and_50_out, and_51_out, and_52_out);
  or or_16 (out_3[7], and_53_out, and_54_out, and_55_out, and_56_out);
  and and_57 (and_57_out, A[8], B[8]);
  and and_58 (and_58_out, or_15_out, B[8]);
  and and_59 (and_59_out, or_15_out, A[8]);
  and and_60 (and_60_out, ~or_15_out, ~A[8], B[8]);  // AND_Gate
  and and_61 (and_61_out, ~or_15_out, A[8], ~B[8]);  // AND_Gate
  and and_62 (and_62_out, or_15_out, ~A[8], ~B[8]);  // AND_Gate
  and and_63 (and_63_out, or_15_out, A[8], B[8]);
  or or_17 (or_17_out, and_57_out, and_58_out, and_59_out);
  or or_18 (out_3[8], and_60_out, and_61_out, and_62_out, and_63_out);
  and and_64 (and_64_out, A[9], B[9]);
  and and_65 (and_65_out, or_17_out, B[9]);
  and and_66 (and_66_out, or_17_out, A[9]);
  and and_67 (and_67_out, ~or_17_out, ~A[9], B[9]);  // AND_Gate
  and and_68 (and_68_out, ~or_17_out, A[9], ~B[9]);  // AND_Gate
  and and_69 (and_69_out, or_17_out, ~A[9], ~B[9]);  // AND_Gate
  and and_70 (and_70_out, or_17_out, A[9], B[9]);
  or or_19 (or_19_out, and_64_out, and_65_out, and_66_out);
  or or_20 (out_3[9], and_67_out, and_68_out, and_69_out, and_70_out);
  and and_71 (and_71_out, A[10], B[10]);
  and and_72 (and_72_out, or_19_out, B[10]);
  and and_73 (and_73_out, or_19_out, A[10]);
  and and_74 (and_74_out, ~or_19_out, ~A[10], B[10]);  // AND_Gate
  and and_75 (and_75_out, ~or_19_out, A[10], ~B[10]);  // AND_Gate
  and and_76 (and_76_out, or_19_out, ~A[10], ~B[10]);  // AND_Gate
  and and_77 (and_77_out, or_19_out, A[10], B[10]);
  or or_21 (or_21_out, and_71_out, and_72_out, and_73_out);
  or or_22 (out_3[10], and_74_out, and_75_out, and_76_out, and_77_out);
  and and_78 (and_78_out, A[11], B[11]);
  and and_79 (and_79_out, or_21_out, B[11]);
  and and_80 (and_80_out, or_21_out, A[11]);
  and and_81 (and_81_out, ~or_21_out, ~A[11], B[11]);  // AND_Gate
  and and_82 (and_82_out, ~or_21_out, A[11], ~B[11]);  // AND_Gate
  and and_83 (and_83_out, or_21_out, ~A[11], ~B[11]);  // AND_Gate
  and and_84 (and_84_out, or_21_out, A[11], B[11]);
  or or_23 (or_23_out, and_78_out, and_79_out, and_80_out);
  or or_24 (out_3[11], and_81_out, and_82_out, and_83_out, and_84_out);
  and and_85 (and_85_out, A[12], B[12]);
  and and_86 (and_86_out, or_23_out, B[12]);
  and and_87 (and_87_out, or_23_out, A[12]);
  and and_88 (and_88_out, ~or_23_out, ~A[12], B[12]);  // AND_Gate
  and and_89 (and_89_out, ~or_23_out, A[12], ~B[12]);  // AND_Gate
  and and_90 (and_90_out, or_23_out, ~A[12], ~B[12]);  // AND_Gate
  and and_91 (and_91_out, or_23_out, A[12], B[12]);
  or or_25 (or_25_out, and_85_out, and_86_out, and_87_out);
  or or_26 (out_3[12], and_88_out, and_89_out, and_90_out, and_91_out);
  and and_92 (and_92_out, A[13], B[13]);
  and and_93 (and_93_out, or_25_out, B[13]);
  and and_94 (and_94_out, or_25_out, A[13]);
  and and_95 (and_95_out, ~or_25_out, ~A[13], B[13]);  // AND_Gate
  and and_96 (and_96_out, ~or_25_out, A[13], ~B[13]);  // AND_Gate
  and and_97 (and_97_out, or_25_out, ~A[13], ~B[13]);  // AND_Gate
  and and_98 (and_98_out, or_25_out, A[13], B[13]);
  or or_27 (or_27_out, and_92_out, and_93_out, and_94_out);
  or or_28 (out_3[13], and_95_out, and_96_out, and_97_out, and_98_out);
  and and_99 (and_99_out, A[14], B[14]);
  and and_100 (and_100_out, or_27_out, B[14]);
  and and_101 (and_101_out, or_27_out, A[14]);
  and and_102 (and_102_out, ~or_27_out, ~A[14], B[14]);  // AND_Gate
  and and_103 (and_103_out, ~or_27_out, A[14], ~B[14]);  // AND_Gate
  and and_104 (and_104_out, or_27_out, ~A[14], ~B[14]);  // AND_Gate
  and and_105 (and_105_out, or_27_out, A[14], B[14]);
  or or_29 (or_29_out, and_99_out, and_100_out, and_101_out);
  or or_30 (out_3[14], and_102_out, and_103_out, and_104_out, and_105_out);
  and and_106 (and_106_out, A[15], B[15]);
  and and_107 (and_107_out, or_29_out, B[15]);
  and and_108 (and_108_out, or_29_out, A[15]);
  and and_109 (and_109_out, ~or_29_out, ~A[15], B[15]);  // AND_Gate
  and and_110 (and_110_out, ~or_29_out, A[15], ~B[15]);  // AND_Gate
  and and_111 (and_111_out, or_29_out, ~A[15], ~B[15]);  // AND_Gate
  and and_112 (and_112_out, or_29_out, A[15], B[15]);
  or or_31 (or_31_out, and_106_out, and_107_out, and_108_out);
  LED led_1 (.in(or_31_out));
  or or_32 (out_3[15], and_109_out, and_110_out, and_111_out, and_112_out);

  // Notes on the sheet:
  //   A: pull=down
  //   B: pull=down
  //   out_3: pull=down
endmodule

module Comp_2_16b (
  input  [15:0] In,
  output [15:0] Out
);

  wire [15:0] extensor_1_16_1_out, not_1_out;

  assign not_1_out = ~In;  // NOT_Gate not_1, 16 bits wide
  Extensor_1_16 extensor_1_16_1 (.In(1'b1), .Out(extensor_1_16_1_out));
  Add_16b add_16b_1 (.A(not_1_out), .B(extensor_1_16_1_out), .out_3(Out));

  // Notes on the sheet:
  //   In: pull=down
  //   Out: pull=down
endmodule

module And (
  input  [15:0] A,
  input  [15:0] B,
  output [15:0] Out
);

  assign Out = A & B;  // AND_Gate and_1, 16 bits wide

  // Notes on the sheet:
  //   Out: pull=down
endmodule

module Or (
  input  [15:0] A,
  input  [15:0] B,
  output [15:0] Out
);

  assign Out = A | B;  // OR_Gate or_1, 16 bits wide

  // Notes on the sheet:
  //   Out: pull=down
endmodule

module Not (
  input  [15:0] A,
  output [15:0] Out
);

  assign Out = ~A;  // NOT_Gate not_1, 16 bits wide

  // Notes on the sheet:
  //   Out: pull=down
endmodule

module Set_less (
  input  [15:0] A,
  input  [15:0] B,
  output [15:0] Out
);

  wire [15:0] add_16b_1_out_3, comp_2_16b_1_out;

  Add_16b add_16b_1 (.A(A), .B(comp_2_16b_1_out), .out_3(add_16b_1_out_3));
  Comp_2_16b comp_2_16b_1 (.In(B), .Out(comp_2_16b_1_out));
  Extensor_1_16 extensor_1_16_1 (.In(add_16b_1_out_3[15]), .Out(Out));

  // Notes on the sheet:
  //   Out: pull=down
endmodule

module ULA (
  input  [2:0] Funct,
  input  [15:0] A,
  input  [15:0] B,
  output [15:0] Out,
  output Zero
);

  wire [15:0] add_16b_1_out_3, and_1_out, not_1_out, not_2_out, or_1_out, set_less_1_out, shift_left_1_out_3,
       shift_right_1_out_3, sub_1_out;

  Add_16b add_16b_1 (.A(A), .B(B), .out_3(add_16b_1_out_3));
  sub sub_1 (.A(A), .B(B), .Out(sub_1_out));
  And and_1 (.A(A), .B(B), .Out(and_1_out));
  Or or_1 (.A(A), .B(B), .Out(or_1_out));
  Not not_1 (.A(A), .Out(not_1_out));
  Set_less set_less_1 (.A(A), .B(B), .Out(set_less_1_out));
  Shift_Left shift_left_1 (.Shift(B), .Number(A), .out_3(shift_left_1_out_3));
  Shift_Right shift_right_1 (.Shift(B), .Number(A), .out_3(shift_right_1_out_3));
  Multiplexador_8x16b multiplexador_8x16b_1 (
    .A(add_16b_1_out_3), .B(sub_1_out), .C(and_1_out), .D(or_1_out), .E(not_1_out), .F(set_less_1_out),
    .G(shift_left_1_out_3), .H(shift_right_1_out_3), .Out(Out), .Funct(Funct));
  assign not_2_out = ~Out;  // NOT_Gate not_2, 16 bits wide
  and and_2 (Zero, not_2_out[0], not_2_out[1], not_2_out[2], not_2_out[3], not_2_out[4], not_2_out[5], not_2_out[6], not_2_out[7], not_2_out[8], not_2_out[9], not_2_out[10], not_2_out[11], not_2_out[12], not_2_out[13], not_2_out[14], not_2_out[15]);

  // Notes on the sheet:
  //   Out: pull=down
  //   A: pull=down
  //   B: pull=down
  //   Zero: pull=down
endmodule

module Extensor_1_16 (
  input  In,
  output [15:0] Out
);

  not not_1 (Out[15], 1'b1);

  assign Out[14:0] = {{14{Out[15]}}, In};

  // Notes on the sheet:
  //   Out: pull=down
endmodule

module Multiplexador_8x16b (
  input  [2:0] Funct,
  input  [15:0] A,
  input  [15:0] B,
  input  [15:0] C,
  input  [15:0] D,
  input  [15:0] E,
  input  [15:0] F,
  input  [15:0] G,
  input  [15:0] H,
  output [15:0] Out
);

  wire multi_a_men_8b_1__0, multi_a_men_8b_1__1, multi_a_men_8b_1__2, multi_a_men_8b_1__3,
       multi_a_men_8b_1__4, multi_a_men_8b_1__5, multi_a_men_8b_1__6, multi_a_men_8b_1__7;
  wire [15:0] select_16b_1_out, select_16b_2_out, select_16b_3_out, select_16b_4_out, select_16b_5_out,
       select_16b_6_out, select_16b_7_out, select_16b_8_out;

  Multi_A_Men_8b multi_a_men_8b_1 (
    .in_1(Funct), ._0(multi_a_men_8b_1__0), ._1(multi_a_men_8b_1__1), ._2(multi_a_men_8b_1__2),
    ._3(multi_a_men_8b_1__3), ._4(multi_a_men_8b_1__4), ._5(multi_a_men_8b_1__5), ._6(multi_a_men_8b_1__6),
    ._7(multi_a_men_8b_1__7));
  Select_16b select_16b_1 (.In(A), .Out(select_16b_1_out), .E(multi_a_men_8b_1__0));
  Select_16b select_16b_2 (.In(B), .Out(select_16b_2_out), .E(multi_a_men_8b_1__1));
  Select_16b select_16b_3 (.In(C), .Out(select_16b_3_out), .E(multi_a_men_8b_1__2));
  Select_16b select_16b_4 (.In(D), .Out(select_16b_4_out), .E(multi_a_men_8b_1__3));
  Select_16b select_16b_5 (.In(E), .Out(select_16b_5_out), .E(multi_a_men_8b_1__4));
  Select_16b select_16b_6 (.In(F), .Out(select_16b_6_out), .E(multi_a_men_8b_1__5));
  Select_16b select_16b_7 (.In(G), .Out(select_16b_7_out), .E(multi_a_men_8b_1__6));
  Select_16b select_16b_8 (.In(H), .Out(select_16b_8_out), .E(multi_a_men_8b_1__7));
  assign Out = select_16b_1_out | select_16b_2_out | select_16b_3_out | select_16b_4_out | select_16b_5_out | select_16b_6_out | select_16b_7_out | select_16b_8_out;  // OR_Gate or_1, 16 bits wide

  // Notes on the sheet:
  //   G: pull=down
  //   F: pull=down
  //   H: pull=down
  //   Out: pull=down
  //   D: pull=down
  //   E: pull=down
  //   Funct: pull=down
  //   B: pull=down
  //   A: pull=down
  //   C: pull=down
endmodule

module Palavra_8b (
  input  [7:0] Data,
  input  CK,
  input  E,
  input  R,
  input  S,
  output [7:0] Out
);

  wire and_1_out, and_2_out, and_3_out, and_4_out, and_5_out, and_6_out, and_7_out, and_8_out, and_9_out,
       and_10_out, and_11_out, and_12_out, and_13_out, and_14_out, and_15_out, and_16_out, and_17_out,
       and_18_out, and_19_out, and_20_out, and_21_out, and_22_out, and_23_out, and_24_out, and_25_out,
       and_26_out, and_27_out, and_28_out, and_29_out, and_30_out, and_31_out, and_32_out, and_33_out,
       and_34_out, and_35_out, and_36_out, and_37_out, and_38_out, and_39_out, and_40_out, nor_1_out,
       nor_2_out, nor_3_out, nor_4_out, nor_5_out, nor_6_out, nor_7_out, nor_8_out, nor_9_out, nor_10_out,
       nor_11_out, nor_12_out, nor_13_out, nor_14_out, nor_15_out, nor_16_out, nor_18_out, nor_20_out,
       nor_22_out, nor_24_out, nor_26_out, nor_28_out, nor_30_out, nor_32_out, not_1_out, not_2_out,
       not_3_out, not_4_out, not_5_out, not_6_out, not_7_out, not_8_out;

  and and_1 (and_1_out, ~Data[0], not_1_out);  // AND_Gate
  not not_1 (not_1_out, and_3_out);
  and and_2 (and_2_out, not_1_out, Data[0]);
  and and_3 (and_3_out, CK, E);
  and and_4 (and_4_out, ~Data[1], not_2_out);  // AND_Gate
  and and_5 (and_5_out, not_2_out, Data[1]);
  not not_2 (not_2_out, and_6_out);
  and and_6 (and_6_out, CK, E);
  and and_7 (and_7_out, ~Data[2], not_3_out);  // AND_Gate
  not not_3 (not_3_out, and_9_out);
  and and_8 (and_8_out, not_3_out, Data[2]);
  and and_9 (and_9_out, CK, E);
  and and_10 (and_10_out, ~Data[3], not_4_out);  // AND_Gate
  and and_11 (and_11_out, not_4_out, Data[3]);
  not not_4 (not_4_out, and_12_out);
  and and_12 (and_12_out, CK, E);
  and and_13 (and_13_out, ~Data[4], not_5_out);  // AND_Gate
  not not_5 (not_5_out, and_15_out);
  and and_14 (and_14_out, not_5_out, Data[4]);
  and and_15 (and_15_out, CK, E);
  and and_16 (and_16_out, ~Data[5], not_6_out);  // AND_Gate
  not not_6 (not_6_out, and_18_out);
  and and_17 (and_17_out, not_6_out, Data[5]);
  and and_18 (and_18_out, CK, E);
  and and_19 (and_19_out, ~Data[6], not_7_out);  // AND_Gate
  and and_20 (and_20_out, not_7_out, Data[6]);
  not not_7 (not_7_out, and_21_out);
  and and_21 (and_21_out, CK, E);
  and and_22 (and_22_out, ~Data[7], not_8_out);  // AND_Gate
  and and_23 (and_23_out, not_8_out, Data[7]);
  not not_8 (not_8_out, and_24_out);
  and and_24 (and_24_out, CK, E);
  nor nor_1 (nor_1_out, R, and_1_out, nor_2_out);
  nor nor_2 (nor_2_out, nor_1_out, and_2_out, S);
  nor nor_3 (nor_3_out, R, and_4_out, nor_4_out);
  nor nor_4 (nor_4_out, nor_3_out, and_5_out, S);
  nor nor_5 (nor_5_out, R, and_7_out, nor_6_out);
  nor nor_6 (nor_6_out, nor_5_out, and_8_out, S);
  nor nor_7 (nor_7_out, R, and_10_out, nor_8_out);
  nor nor_8 (nor_8_out, nor_7_out, and_11_out, S);
  nor nor_9 (nor_9_out, R, and_13_out, nor_10_out);
  nor nor_10 (nor_10_out, nor_9_out, and_14_out, S);
  nor nor_11 (nor_11_out, R, and_16_out, nor_12_out);
  nor nor_12 (nor_12_out, nor_11_out, and_17_out, S);
  nor nor_13 (nor_13_out, R, and_19_out, nor_14_out);
  nor nor_14 (nor_14_out, nor_13_out, and_20_out, S);
  nor nor_15 (nor_15_out, R, and_22_out, nor_16_out);
  nor nor_16 (nor_16_out, nor_15_out, and_23_out, S);
  and and_25 (and_25_out, ~nor_1_out, and_3_out);  // AND_Gate
  and and_26 (and_26_out, and_3_out, nor_1_out);
  and and_27 (and_27_out, ~nor_3_out, and_6_out);  // AND_Gate
  and and_28 (and_28_out, and_6_out, nor_3_out);
  and and_29 (and_29_out, ~nor_5_out, and_9_out);  // AND_Gate
  and and_30 (and_30_out, and_9_out, nor_5_out);
  and and_31 (and_31_out, ~nor_7_out, and_12_out);  // AND_Gate
  and and_32 (and_32_out, and_12_out, nor_7_out);
  and and_33 (and_33_out, ~nor_9_out, and_15_out);  // AND_Gate
  and and_34 (and_34_out, and_15_out, nor_9_out);
  and and_35 (and_35_out, ~nor_11_out, and_18_out);  // AND_Gate
  and and_36 (and_36_out, and_18_out, nor_11_out);
  and and_37 (and_37_out, ~nor_13_out, and_21_out);  // AND_Gate
  and and_38 (and_38_out, and_21_out, nor_13_out);
  and and_39 (and_39_out, ~nor_15_out, and_24_out);  // AND_Gate
  and and_40 (and_40_out, and_24_out, nor_15_out);
  nor nor_17 (Out[0], R, and_25_out, nor_18_out);
  nor nor_18 (nor_18_out, Out[0], and_26_out, S);
  nor nor_19 (Out[1], R, and_27_out, nor_20_out);
  nor nor_20 (nor_20_out, Out[1], and_28_out, S);
  nor nor_21 (Out[2], R, and_29_out, nor_22_out);
  nor nor_22 (nor_22_out, Out[2], and_30_out, S);
  nor nor_23 (Out[3], R, and_31_out, nor_24_out);
  nor nor_24 (nor_24_out, Out[3], and_32_out, S);
  nor nor_25 (Out[4], R, and_33_out, nor_26_out);
  nor nor_26 (nor_26_out, Out[4], and_34_out, S);
  nor nor_27 (Out[5], R, and_35_out, nor_28_out);
  nor nor_28 (nor_28_out, Out[5], and_36_out, S);
  nor nor_29 (Out[6], R, and_37_out, nor_30_out);
  nor nor_30 (nor_30_out, Out[6], and_38_out, S);
  nor nor_31 (Out[7], R, and_39_out, nor_32_out);
  nor nor_32 (nor_32_out, Out[7], and_40_out, S);

  // Notes on the sheet:
  //   R: pull=down
  //   Out: pull=down
  //   Data: pull=down
  //   CK: pull=down
  //   S: pull=down
  //   E: pull=down
endmodule

module Registers_Made_by_me (
  input  Enable_write,
  input  Clock,
  input  [2:0] Rs,
  input  [2:0] Rt,
  input  R,
  input  S,
  input  [2:0] Rd,
  input  [15:0] Write_data,
  output [15:0] Out_1,
  output [15:0] Out_2
);

  Memoria_8x16b memoria_8x16b_1 (
    .S(S), .R(R), .Cl(Clock), .W(Enable_write), .Data(Write_data), .Andress(Rd), .Rs(Rs), .Out_1(Out_1),
    .Rt(Rt), .Out_2(Out_2));

  // Notes on the sheet:
  //   Out_1: pull=down
  //   Out_2: pull=down
endmodule

module PC (
  input  [15:0] Data,
  input  CK,
  input  E,
  input  R,
  input  S,
  output [15:0] Out
);

  wire and_1_out, and_2_out, and_3_out, and_4_out, and_5_out, and_6_out, and_7_out, and_8_out, and_9_out,
       and_10_out, and_11_out, and_12_out, and_13_out, and_14_out, and_15_out, and_16_out, and_17_out,
       and_18_out, and_19_out, and_20_out, and_21_out, and_22_out, and_23_out, and_24_out, and_25_out,
       and_26_out, and_27_out, and_28_out, and_29_out, and_30_out, and_31_out, and_32_out, and_33_out,
       and_34_out, and_35_out, and_36_out, and_37_out, and_38_out, and_39_out, and_40_out, and_41_out,
       and_42_out, and_43_out, and_44_out, and_45_out, and_46_out, and_47_out, and_48_out, and_49_out,
       and_50_out, and_51_out, and_52_out, and_53_out, and_54_out, and_55_out, and_56_out, and_57_out,
       and_58_out, and_59_out, and_60_out, and_61_out, and_62_out, and_63_out, and_64_out, and_65_out,
       and_66_out, and_67_out, and_68_out, and_69_out, and_70_out, and_71_out, and_72_out, and_73_out,
       and_74_out, and_75_out, and_76_out, and_77_out, and_78_out, and_79_out, and_80_out, nor_1_out,
       nor_2_out, nor_3_out, nor_4_out, nor_5_out, nor_6_out, nor_7_out, nor_8_out, nor_9_out, nor_10_out,
       nor_11_out, nor_12_out, nor_13_out, nor_14_out, nor_15_out, nor_16_out, nor_17_out, nor_18_out,
       nor_19_out, nor_20_out, nor_21_out, nor_22_out, nor_23_out, nor_24_out, nor_25_out, nor_26_out,
       nor_27_out, nor_28_out, nor_29_out, nor_30_out, nor_31_out, nor_32_out, nor_34_out, nor_36_out,
       nor_38_out, nor_40_out, nor_42_out, nor_44_out, nor_46_out, nor_48_out, nor_50_out, nor_52_out,
       nor_54_out, nor_56_out, nor_58_out, nor_60_out, nor_62_out, nor_64_out, not_1_out, not_2_out,
       not_3_out, not_4_out, not_5_out, not_6_out, not_7_out, not_8_out, not_9_out, not_10_out, not_11_out,
       not_12_out, not_13_out, not_14_out, not_15_out, not_16_out;

  not not_1 (not_1_out, and_1_out);
  and and_1 (and_1_out, CK, E);
  not not_2 (not_2_out, and_2_out);
  and and_2 (and_2_out, CK, E);
  not not_3 (not_3_out, and_3_out);
  and and_3 (and_3_out, CK, E);
  not not_4 (not_4_out, and_4_out);
  and and_4 (and_4_out, CK, E);
  not not_5 (not_5_out, and_5_out);
  and and_5 (and_5_out, CK, E);
  not not_6 (not_6_out, and_6_out);
  and and_6 (and_6_out, CK, E);
  and and_7 (and_7_out, ~Data[6], not_7_out);  // AND_Gate
  not not_7 (not_7_out, and_9_out);
  and and_8 (and_8_out, not_7_out, Data[6]);
  and and_9 (and_9_out, CK, E);
  and and_10 (and_10_out, ~Data[7], not_8_out);  // AND_Gate
  not not_8 (not_8_out, and_12_out);
  and and_11 (and_11_out, not_8_out, Data[7]);
  and and_12 (and_12_out, CK, E);
  and and_13 (and_13_out, ~Data[8], not_9_out);  // AND_Gate
  and and_14 (and_14_out, not_9_out, Data[8]);
  not not_9 (not_9_out, and_15_out);
  and and_15 (and_15_out, CK, E);
  and and_16 (and_16_out, ~Data[9], not_10_out);  // AND_Gate
  not not_10 (not_10_out, and_18_out);
  and and_17 (and_17_out, not_10_out, Data[9]);
  and and_18 (and_18_out, CK, E);
  and and_19 (and_19_out, ~Data[10], not_11_out);  // AND_Gate
  and and_20 (and_20_out, not_11_out, Data[10]);
  not not_11 (not_11_out, and_21_out);
  and and_21 (and_21_out, CK, E);
  and and_22 (and_22_out, ~Data[11], not_12_out);  // AND_Gate
  and and_23 (and_23_out, not_12_out, Data[11]);
  not not_12 (not_12_out, and_24_out);
  and and_24 (and_24_out, CK, E);
  and and_25 (and_25_out, ~Data[12], not_13_out);  // AND_Gate
  and and_26 (and_26_out, not_13_out, Data[12]);
  not not_13 (not_13_out, and_27_out);
  and and_27 (and_27_out, CK, E);
  and and_28 (and_28_out, ~Data[13], not_14_out);  // AND_Gate
  not not_14 (not_14_out, and_30_out);
  and and_29 (and_29_out, not_14_out, Data[13]);
  and and_30 (and_30_out, CK, E);
  and and_31 (and_31_out, ~Data[14], not_15_out);  // AND_Gate
  and and_32 (and_32_out, not_15_out, Data[14]);
  not not_15 (not_15_out, and_33_out);
  and and_33 (and_33_out, CK, E);
  and and_34 (and_34_out, ~Data[15], not_16_out);  // AND_Gate
  and and_35 (and_35_out, not_16_out, Data[15]);
  not not_16 (not_16_out, and_36_out);
  and and_36 (and_36_out, CK, E);
  nor nor_1 (nor_1_out, R, and_37_out, nor_2_out);
  and and_37 (and_37_out, ~Data[0], not_1_out);  // AND_Gate
  nor nor_2 (nor_2_out, nor_1_out, and_38_out, S);
  and and_38 (and_38_out, not_1_out, Data[0]);
  and and_39 (and_39_out, ~Data[1], not_2_out);  // AND_Gate
  nor nor_3 (nor_3_out, R, and_39_out, nor_4_out);
  nor nor_4 (nor_4_out, nor_3_out, and_40_out, S);
  and and_40 (and_40_out, not_2_out, Data[1]);
  and and_41 (and_41_out, ~Data[2], not_3_out);  // AND_Gate
  nor nor_5 (nor_5_out, R, and_41_out, nor_6_out);
  and and_42 (and_42_out, not_3_out, Data[2]);
  nor nor_6 (nor_6_out, nor_5_out, and_42_out, S);
  and and_43 (and_43_out, ~Data[3], not_4_out);  // AND_Gate
  nor nor_7 (nor_7_out, R, and_43_out, nor_8_out);
  nor nor_8 (nor_8_out, nor_7_out, and_44_out, S);
  and and_44 (and_44_out, not_4_out, Data[3]);
  and and_45 (and_45_out, ~Data[4], not_5_out);  // AND_Gate
  nor nor_9 (nor_9_out, R, and_45_out, nor_10_out);
  nor nor_10 (nor_10_out, nor_9_out, and_46_out, S);
  and and_46 (and_46_out, not_5_out, Data[4]);
  nor nor_11 (nor_11_out, R, and_47_out, nor_12_out);
  and and_47 (and_47_out, ~Data[5], not_6_out);  // AND_Gate
  and and_48 (and_48_out, not_6_out, Data[5]);
  nor nor_12 (nor_12_out, nor_11_out, and_48_out, S);
  nor nor_13 (nor_13_out, R, and_7_out, nor_14_out);
  nor nor_14 (nor_14_out, nor_13_out, and_8_out, S);
  nor nor_15 (nor_15_out, R, and_10_out, nor_16_out);
  nor nor_16 (nor_16_out, nor_15_out, and_11_out, S);
  nor nor_17 (nor_17_out, R, and_13_out, nor_18_out);
  nor nor_18 (nor_18_out, nor_17_out, and_14_out, S);
  nor nor_19 (nor_19_out, R, and_16_out, nor_20_out);
  nor nor_20 (nor_20_out, nor_19_out, and_17_out, S);
  nor nor_21 (nor_21_out, R, and_19_out, nor_22_out);
  nor nor_22 (nor_22_out, nor_21_out, and_20_out, S);
  nor nor_23 (nor_23_out, R, and_22_out, nor_24_out);
  nor nor_24 (nor_24_out, nor_23_out, and_23_out, S);
  nor nor_25 (nor_25_out, R, and_25_out, nor_26_out);
  nor nor_26 (nor_26_out, nor_25_out, and_26_out, S);
  nor nor_27 (nor_27_out, R, and_28_out, nor_28_out);
  nor nor_28 (nor_28_out, nor_27_out, and_29_out, S);
  nor nor_29 (nor_29_out, R, and_31_out, nor_30_out);
  nor nor_30 (nor_30_out, nor_29_out, and_32_out, S);
  nor nor_31 (nor_31_out, R, and_34_out, nor_32_out);
  nor nor_32 (nor_32_out, nor_31_out, and_35_out, S);
  and and_49 (and_49_out, ~nor_1_out, and_1_out);  // AND_Gate
  and and_50 (and_50_out, and_1_out, nor_1_out);
  and and_51 (and_51_out, ~nor_3_out, and_2_out);  // AND_Gate
  and and_52 (and_52_out, and_2_out, nor_3_out);
  and and_53 (and_53_out, ~nor_5_out, and_3_out);  // AND_Gate
  and and_54 (and_54_out, and_3_out, nor_5_out);
  and and_55 (and_55_out, ~nor_7_out, and_4_out);  // AND_Gate
  and and_56 (and_56_out, and_4_out, nor_7_out);
  and and_57 (and_57_out, ~nor_9_out, and_5_out);  // AND_Gate
  and and_58 (and_58_out, and_5_out, nor_9_out);
  and and_59 (and_59_out, ~nor_11_out, and_6_out);  // AND_Gate
  and and_60 (and_60_out, and_6_out, nor_11_out);
  and and_61 (and_61_out, ~nor_13_out, and_9_out);  // AND_Gate
  and and_62 (and_62_out, and_9_out, nor_13_out);
  and and_63 (and_63_out, ~nor_15_out, and_12_out);  // AND_Gate
  and and_64 (and_64_out, and_12_out, nor_15_out);
  and and_65 (and_65_out, ~nor_17_out, and_15_out);  // AND_Gate
  and and_66 (and_66_out, and_15_out, nor_17_out);
  and and_67 (and_67_out, ~nor_19_out, and_18_out);  // AND_Gate
  and and_68 (and_68_out, and_18_out, nor_19_out);
  and and_69 (and_69_out, ~nor_21_out, and_21_out);  // AND_Gate
  and and_70 (and_70_out, and_21_out, nor_21_out);
  and and_71 (and_71_out, ~nor_23_out, and_24_out);  // AND_Gate
  and and_72 (and_72_out, and_24_out, nor_23_out);
  and and_73 (and_73_out, ~nor_25_out, and_27_out);  // AND_Gate
  and and_74 (and_74_out, and_27_out, nor_25_out);
  and and_75 (and_75_out, ~nor_27_out, and_30_out);  // AND_Gate
  and and_76 (and_76_out, and_30_out, nor_27_out);
  and and_77 (and_77_out, ~nor_29_out, and_33_out);  // AND_Gate
  and and_78 (and_78_out, and_33_out, nor_29_out);
  and and_79 (and_79_out, ~nor_31_out, and_36_out);  // AND_Gate
  and and_80 (and_80_out, and_36_out, nor_31_out);
  nor nor_33 (Out[0], R, and_49_out, nor_34_out);
  nor nor_34 (nor_34_out, Out[0], and_50_out, S);
  nor nor_35 (Out[1], R, and_51_out, nor_36_out);
  nor nor_36 (nor_36_out, Out[1], and_52_out, S);
  nor nor_37 (Out[2], R, and_53_out, nor_38_out);
  nor nor_38 (nor_38_out, Out[2], and_54_out, S);
  nor nor_39 (Out[3], R, and_55_out, nor_40_out);
  nor nor_40 (nor_40_out, Out[3], and_56_out, S);
  nor nor_41 (Out[4], R, and_57_out, nor_42_out);
  nor nor_42 (nor_42_out, Out[4], and_58_out, S);
  nor nor_43 (Out[5], R, and_59_out, nor_44_out);
  nor nor_44 (nor_44_out, Out[5], and_60_out, S);
  nor nor_45 (Out[6], R, and_61_out, nor_46_out);
  nor nor_46 (nor_46_out, Out[6], and_62_out, S);
  nor nor_47 (Out[7], R, and_63_out, nor_48_out);
  nor nor_48 (nor_48_out, Out[7], and_64_out, S);
  nor nor_49 (Out[8], R, and_65_out, nor_50_out);
  nor nor_50 (nor_50_out, Out[8], and_66_out, S);
  nor nor_51 (Out[9], R, and_67_out, nor_52_out);
  nor nor_52 (nor_52_out, Out[9], and_68_out, S);
  nor nor_53 (Out[10], R, and_69_out, nor_54_out);
  nor nor_54 (nor_54_out, Out[10], and_70_out, S);
  nor nor_55 (Out[11], R, and_71_out, nor_56_out);
  nor nor_56 (nor_56_out, Out[11], and_72_out, S);
  nor nor_57 (Out[12], R, and_73_out, nor_58_out);
  nor nor_58 (nor_58_out, Out[12], and_74_out, S);
  nor nor_59 (Out[13], R, and_75_out, nor_60_out);
  nor nor_60 (nor_60_out, Out[13], and_76_out, S);
  nor nor_61 (Out[14], R, and_77_out, nor_62_out);
  nor nor_62 (nor_62_out, Out[14], and_78_out, S);
  nor nor_63 (Out[15], R, and_79_out, nor_64_out);
  nor nor_64 (nor_64_out, Out[15], and_80_out, S);

  // Notes on the sheet:
  //   E: pull=down
  //   Data: pull=down
  //   Out: pull=down
  //   CK: pull=down
  //   R: pull=down
  //   S: pull=down
endmodule

module Bit (
  input  R,
  input  D,
  input  CK,
  input  E,
  input  S,
  output Q
);

  wire and_1_out, and_2_out, and_3_out, and_4_out, and_5_out, nor_1_out, nor_2_out, nor_4_out, not_1_out;

  and and_1 (and_1_out, CK, E);
  not not_1 (not_1_out, and_1_out);
  and and_2 (and_2_out, ~D, not_1_out);  // AND_Gate
  and and_3 (and_3_out, not_1_out, D);
  nor nor_1 (nor_1_out, R, and_2_out, nor_2_out);
  nor nor_2 (nor_2_out, nor_1_out, and_3_out, S);
  and and_4 (and_4_out, ~nor_1_out, and_1_out);  // AND_Gate
  and and_5 (and_5_out, and_1_out, nor_1_out);
  nor nor_3 (Q, R, and_4_out, nor_4_out);
  nor nor_4 (nor_4_out, Q, and_5_out, S);

  // Notes on the sheet:
  //   R: pull=down
  //   D: pull=down
  //   S: pull=down
  //   Q: pull=down
  //   CK: pull=down
  //   E: pull=down
endmodule

module Calc (
  input  [15:0] in_1,
  input  [15:0] in_2
);

  wire [7:0] ctrl_display_d_1_out_2, ctrl_display_d_2_out_2, ctrl_display_d_3_out_2, ctrl_display_u_1_out_2,
       ctrl_display_u_2_out_2, ctrl_display_u_3_out_2;
  wire [15:0] add_16b_1_out_3, comp_2_16b_1_out;

  Comp_2_16b comp_2_16b_1 (.In(in_2), .Out(comp_2_16b_1_out));
  Add_16b add_16b_1 (.A(in_1), .B(comp_2_16b_1_out), .out_3(add_16b_1_out_3));
  Ctrl_Display_U ctrl_display_u_1 (.in_1(in_1[3:0]), .out_2(ctrl_display_u_1_out_2));
  Ctrl_Display_D ctrl_display_d_1 (.in_1(in_1[3:0]), .out_2(ctrl_display_d_1_out_2));
  _7_Segment_Display u_7_segment_display_1 (
    .g(ctrl_display_d_1_out_2[3]), .f(ctrl_display_d_1_out_2[2]), .a(ctrl_display_d_1_out_2[1]),
    .b(ctrl_display_d_1_out_2[0]), .e(ctrl_display_d_1_out_2[7]), .d(ctrl_display_d_1_out_2[6]),
    .c(ctrl_display_d_1_out_2[5]), .dp(ctrl_display_d_1_out_2[4]));
  Ctrl_Display_U ctrl_display_u_2 (.in_1(in_2[3:0]), .out_2(ctrl_display_u_2_out_2));
  Ctrl_Display_D ctrl_display_d_2 (.in_1(in_2[3:0]), .out_2(ctrl_display_d_2_out_2));
  _7_Segment_Display u_7_segment_display_2 (
    .g(ctrl_display_d_2_out_2[3]), .f(ctrl_display_d_2_out_2[2]), .a(ctrl_display_d_2_out_2[1]),
    .b(ctrl_display_d_2_out_2[0]), .e(ctrl_display_d_2_out_2[7]), .d(ctrl_display_d_2_out_2[6]),
    .c(ctrl_display_d_2_out_2[5]), .dp(ctrl_display_d_2_out_2[4]));
  Ctrl_Display_U ctrl_display_u_3 (.in_1(add_16b_1_out_3[3:0]), .out_2(ctrl_display_u_3_out_2));
  Ctrl_Display_D ctrl_display_d_3 (.in_1(add_16b_1_out_3[3:0]), .out_2(ctrl_display_d_3_out_2));
  _7_Segment_Display u_7_segment_display_3 (
    .g(ctrl_display_d_3_out_2[3]), .f(ctrl_display_d_3_out_2[2]), .a(ctrl_display_d_3_out_2[1]),
    .b(ctrl_display_d_3_out_2[0]), .e(ctrl_display_d_3_out_2[7]), .d(ctrl_display_d_3_out_2[6]),
    .c(ctrl_display_d_3_out_2[5]), .dp(ctrl_display_d_3_out_2[4]));
  _7_Segment_Display u_7_segment_display_4 (
    .g(ctrl_display_u_1_out_2[3]), .f(ctrl_display_u_1_out_2[2]), .a(ctrl_display_u_1_out_2[1]),
    .b(ctrl_display_u_1_out_2[0]), .e(ctrl_display_u_1_out_2[7]), .d(ctrl_display_u_1_out_2[6]),
    .c(ctrl_display_u_1_out_2[5]), .dp(ctrl_display_u_1_out_2[4]));
  _7_Segment_Display u_7_segment_display_5 (
    .g(ctrl_display_u_2_out_2[3]), .f(ctrl_display_u_2_out_2[2]), .a(ctrl_display_u_2_out_2[1]),
    .b(ctrl_display_u_2_out_2[0]), .e(ctrl_display_u_2_out_2[7]), .d(ctrl_display_u_2_out_2[6]),
    .c(ctrl_display_u_2_out_2[5]), .dp(ctrl_display_u_2_out_2[4]));
  _7_Segment_Display u_7_segment_display_6 (
    .g(ctrl_display_u_3_out_2[3]), .f(ctrl_display_u_3_out_2[2]), .a(ctrl_display_u_3_out_2[1]),
    .b(ctrl_display_u_3_out_2[0]), .e(ctrl_display_u_3_out_2[7]), .d(ctrl_display_u_3_out_2[6]),
    .c(ctrl_display_u_3_out_2[5]), .dp(ctrl_display_u_3_out_2[4]));
endmodule

module RAM (
  input  [15:0] in_1,
  input  Store,
  input  [15:0] in_3,
  input  in_4,
  input  [15:0] in_5,
  input  [15:0] in_6,
  input  Store_2,
  input  in_8,
  input  in_9,
  input  [2:0] in_10,
  input  [2:0] in_11,
  input  [2:0] in_12,
  input  [15:0] in_13,
  output [15:0] Out,
  output [15:0] Out_2,
  output [15:0] Out_3,
  output [15:0] Out_4
);

  wire clock_1_out, clock_2_out, not_1_out, not_2_out, registers_1_p6, registers_1_p7;

  assign Out = Store ? in_1 : 16'bz;  // Controlled_Buffer controlled_buffer_1
  not not_1 (not_1_out, Store);
  Clock clock_1 (.out(clock_1_out));
  not not_2 (not_2_out, Store_2);
  Clock clock_2 (.out(clock_2_out));
  // Registers registers_1: pin names not known; wires that end beside it: in_10, in_11, in_12, in_13, in_9, registers_1_p6, registers_1_p7, Out_3, Out_4
  Button Cls (.out(registers_1_p7));
  Clock clock_3 (.out(registers_1_p6));
  RAM_part #(.addrWidth(16), .dataWidth(16), .bus("asynch")) ram_1 (
    .addr(in_3), .data(Out), .sel(clock_1_out), .ld(not_1_out), .clr(in_4));
  RAM_part #(.addrWidth(16), .dataWidth(16), .bus("separate")) ram_2 (
    .addr(in_5), .din(in_6), .data(Out_2), .str(Store_2), .sel(clock_2_out), .clk(clock_2_out),
    .ld(not_2_out), .clr(in_8));

  // Notes on the sheet:
  //   in_11: pull=down
  //   Out_4: pull=down
  //   Out: pull=down
  //   in_10: pull=down
  //   Out_3: pull=down
  //   Out_2: pull=down
  //   in_12: pull=down
endmodule

module Start_Pause (
  input  Start,
  input  Pause,
  output Q
);

  wire nor_2_out;

  nor nor_1 (Q, Pause, nor_2_out);
  nor nor_2 (nor_2_out, Q, Start);

  // Notes on the sheet:
  //   Q: pull=down
  //   Pause: pull=down
  //   Start: pull=down
endmodule

module Multiplexador_2x3b (
  input  Op,
  input  [2:0] _0,
  input  [2:0] _1,
  output [2:0] Out
);

  wire [2:0] and_1_out, and_4_out;

  and and_1 (and_1_out[0], _0[0], ~Op);  // AND_Gate
  and and_2 (and_1_out[1], _0[1], ~Op);  // AND_Gate
  and and_3 (and_1_out[2], _0[2], ~Op);  // AND_Gate
  and and_4 (and_4_out[0], _1[0], Op);
  and and_5 (and_4_out[1], _1[1], Op);
  and and_6 (and_4_out[2], _1[2], Op);
  assign Out = and_1_out | and_4_out;  // OR_Gate or_1, 3 bits wide

  // Notes on the sheet:
  //   Out: pull=down
endmodule

module Multiplexador_2x16b (
  input  Op,
  input  Op_2,
  input  [15:0] _0,
  input  [15:0] _1,
  output [15:0] Out
);

  wire or_1_out;
  wire [15:0] and_1_out, and_17_out;

  or or_1 (or_1_out, Op, Op_2);
  and and_1 (and_1_out[0], _0[0], ~or_1_out);  // AND_Gate
  and and_2 (and_1_out[1], _0[1], ~or_1_out);  // AND_Gate
  and and_3 (and_1_out[2], _0[2], ~or_1_out);  // AND_Gate
  and and_4 (and_1_out[3], _0[3], ~or_1_out);  // AND_Gate
  and and_5 (and_1_out[4], _0[4], ~or_1_out);  // AND_Gate
  and and_6 (and_1_out[5], _0[5], ~or_1_out);  // AND_Gate
  and and_7 (and_1_out[6], _0[6], ~or_1_out);  // AND_Gate
  and and_8 (and_1_out[7], _0[7], ~or_1_out);  // AND_Gate
  and and_9 (and_1_out[8], _0[8], ~or_1_out);  // AND_Gate
  and and_10 (and_1_out[9], _0[9], ~or_1_out);  // AND_Gate
  and and_11 (and_1_out[10], _0[10], ~or_1_out);  // AND_Gate
  and and_12 (and_1_out[11], _0[11], ~or_1_out);  // AND_Gate
  and and_13 (and_1_out[12], _0[12], ~or_1_out);  // AND_Gate
  and and_14 (and_1_out[13], _0[13], ~or_1_out);  // AND_Gate
  and and_15 (and_1_out[14], _0[14], ~or_1_out);  // AND_Gate
  and and_16 (and_1_out[15], _0[15], ~or_1_out);  // AND_Gate
  and and_17 (and_17_out[0], _1[0], or_1_out);
  and and_18 (and_17_out[1], _1[1], or_1_out);
  and and_19 (and_17_out[2], _1[2], or_1_out);
  and and_20 (and_17_out[3], _1[3], or_1_out);
  and and_21 (and_17_out[4], _1[4], or_1_out);
  and and_22 (and_17_out[5], _1[5], or_1_out);
  and and_23 (and_17_out[6], _1[6], or_1_out);
  and and_24 (and_17_out[7], _1[7], or_1_out);
  and and_25 (and_17_out[8], _1[8], or_1_out);
  and and_26 (and_17_out[9], _1[9], or_1_out);
  and and_27 (and_17_out[10], _1[10], or_1_out);
  and and_28 (and_17_out[11], _1[11], or_1_out);
  and and_29 (and_17_out[12], _1[12], or_1_out);
  and and_30 (and_17_out[13], _1[13], or_1_out);
  and and_31 (and_17_out[14], _1[14], or_1_out);
  and and_32 (and_17_out[15], _1[15], or_1_out);
  assign Out = and_1_out | and_17_out;  // OR_Gate or_2, 16 bits wide

  // Notes on the sheet:
  //   Op_2: pull=down
  //   Op: pull=down
  //   Out: pull=down
  //   _1: pull=down
  //   _0: pull=down
endmodule

module Extensor_6_16 (
  input  [5:0] In,
  output [15:0] Out
);

  not not_1 (Out[15], 1'b1);

  assign Out[14:0] = {{9{Out[15]}}, In};

  // Notes on the sheet:
  //   Out: pull=down
endmodule

module AluCtrl (
  input  [1:0] AluOp,
  input  [2:0] Funct,
  output [2:0] out_3
);

  wire [2:0] and_1_out, and_4_out;

  and and_1 (and_1_out[0], Funct[0], ~AluOp[1], ~AluOp[0]);  // AND_Gate
  and and_2 (and_1_out[1], Funct[1], ~AluOp[1], ~AluOp[0]);  // AND_Gate
  and and_3 (and_1_out[2], Funct[2], ~AluOp[1], ~AluOp[0]);  // AND_Gate
  and and_4 (and_4_out[0], AluOp[1], AluOp[1], ~AluOp[0]);  // AND_Gate
  and and_5 (and_4_out[1], AluOp[1], AluOp[0], ~AluOp[0]);  // AND_Gate
  and and_6 (and_4_out[2], AluOp[1], AluOp[0], ~AluOp[0]);  // AND_Gate
  assign out_3 = and_1_out | and_4_out;  // OR_Gate or_1, 3 bits wide

  // Notes on the sheet:
  //   out_3: pull=down
  //   Funct: pull=down
  //   AluOp: pull=down
endmodule

// Ctrl
module Unidade_Controle (
  input  [3:0] OpCode,
  output RgDst,
  output MemoReg,
  output Jump,
  output StoreGraphics,
  output LoadBuffer,
  output Branch,
  output MemWrite,
  output [1:0] AluOp,
  output AluSrc,
  output RegWrite,
  output PcPause
);

  wire and_2_out, and_3_out, and_4_out, and_5_out, and_6_out, and_12_out;

  and and_1 (RgDst, ~OpCode[3], ~OpCode[2], ~OpCode[0]);  // AND_Gate
  or or_1 (MemoReg, ~OpCode[0], OpCode[1]);  // OR_Gate
  and and_2 (and_2_out, ~OpCode[2], OpCode[0]);  // AND_Gate
  and and_3 (and_3_out, ~OpCode[2], OpCode[0]);  // AND_Gate
  and and_4 (and_4_out, OpCode[2], ~OpCode[0]);  // AND_Gate
  and and_5 (and_5_out, ~OpCode[3], ~OpCode[1], ~OpCode[0]);  // AND_Gate
  and and_6 (and_6_out, ~OpCode[3], ~OpCode[2], OpCode[0]);  // AND_Gate
  and and_7 (Jump, ~OpCode[3], OpCode[2], OpCode[1], ~OpCode[0]);  // AND_Gate
  and and_8 (StoreGraphics, OpCode[3], ~OpCode[2], ~OpCode[1], OpCode[0]);  // AND_Gate
  and and_9 (LoadBuffer, OpCode[3], ~OpCode[2], OpCode[1], ~OpCode[0]);  // AND_Gate
  and and_10 (Branch, ~OpCode[3], OpCode[2], ~OpCode[1], OpCode[0]);  // AND_Gate
  and and_11 (MemWrite, ~OpCode[3], ~OpCode[2], OpCode[1], ~OpCode[0]);  // AND_Gate
  or or_2 (AluOp[0], OpCode[1], and_2_out);
  or or_3 (AluSrc, OpCode[1], and_3_out, and_4_out);
  or or_4 (RegWrite, and_5_out, and_6_out, and_12_out);
  and and_12 (and_12_out, OpCode[3], ~OpCode[2], OpCode[1], ~OpCode[0]);  // AND_Gate
  and and_13 (PcPause, OpCode[3], OpCode[2], OpCode[1], OpCode[0]);

  assign AluOp[1] = OpCode[2];

  // Notes on the sheet:
  //   StoreGraphics: pull=down
  //   Branch: pull=down
  //   OpCode: pull=down
  //   RegWrite: pull=down
  //   MemoReg: pull=down
  //   AluSrc: pull=down
  //   AluOp: pull=down
  //   MemWrite: pull=down
  //   PcPause: pull=down
  //   Jump: pull=down
  //   RgDst: pull=down
  //   LoadBuffer: pull=down
endmodule
module Registers (
  input  R,
  input  Clock,
  input  [15:0] Write_data,
  input  Enable_write,
  input  [2:0] Rd,
  input  [2:0] Rs,
  input  [2:0] Rt,
  output [15:0] Out_1,
  output [15:0] Out_2
);

  wire and_1_out, and_2_out, and_3_out, and_4_out, and_5_out, and_6_out, and_7_out, and_8_out,
       multi_a_men_8b_1__0, multi_a_men_8b_1__1, multi_a_men_8b_1__2, multi_a_men_8b_1__3,
       multi_a_men_8b_1__4, multi_a_men_8b_1__5, multi_a_men_8b_1__6, multi_a_men_8b_1__7,
       multi_a_men_8b_2__0, multi_a_men_8b_2__1, multi_a_men_8b_2__2, multi_a_men_8b_2__3,
       multi_a_men_8b_2__4, multi_a_men_8b_2__5, multi_a_men_8b_2__6, multi_a_men_8b_2__7,
       multi_a_men_8b_3__0, multi_a_men_8b_3__1, multi_a_men_8b_3__2, multi_a_men_8b_3__3,
       multi_a_men_8b_3__4, multi_a_men_8b_3__5, multi_a_men_8b_3__6, multi_a_men_8b_3__7;
  wire [15:0] _0, _1, _2, _3, _4, _5, _6, _7, controlled_buffer_1_out, controlled_buffer_2_out,
       controlled_buffer_3_out, controlled_buffer_4_out, controlled_buffer_5_out, controlled_buffer_6_out,
       controlled_buffer_7_out, controlled_buffer_8_out, controlled_buffer_9_out, controlled_buffer_10_out,
       controlled_buffer_11_out, controlled_buffer_12_out, controlled_buffer_13_out,
       controlled_buffer_14_out, controlled_buffer_15_out, controlled_buffer_16_out;

  and and_1 (and_1_out, Enable_write, multi_a_men_8b_1__0);
  Multi_A_Men_8b multi_a_men_8b_1 (
    .in_1(Rd), ._0(multi_a_men_8b_1__0), ._1(multi_a_men_8b_1__1), ._2(multi_a_men_8b_1__2),
    ._3(multi_a_men_8b_1__3), ._4(multi_a_men_8b_1__4), ._5(multi_a_men_8b_1__5), ._6(multi_a_men_8b_1__6),
    ._7(multi_a_men_8b_1__7));
  Multi_A_Men_8b multi_a_men_8b_2 (
    .in_1(Rs), ._0(multi_a_men_8b_2__0), ._1(multi_a_men_8b_2__1), ._2(multi_a_men_8b_2__2),
    ._3(multi_a_men_8b_2__3), ._4(multi_a_men_8b_2__4), ._5(multi_a_men_8b_2__5), ._6(multi_a_men_8b_2__6),
    ._7(multi_a_men_8b_2__7));
  Multi_A_Men_8b multi_a_men_8b_3 (
    .in_1(Rt), ._0(multi_a_men_8b_3__0), ._1(multi_a_men_8b_3__1), ._2(multi_a_men_8b_3__2),
    ._3(multi_a_men_8b_3__3), ._4(multi_a_men_8b_3__4), ._5(multi_a_men_8b_3__5), ._6(multi_a_men_8b_3__6),
    ._7(multi_a_men_8b_3__7));
  Register #(.width(16)) register_1 (.D(Write_data), .en(and_1_out), .Q(_0), .clk(Clock), .clr(R));
  assign controlled_buffer_1_out = multi_a_men_8b_2__0 ? _0 : 16'bz;  // Controlled_Buffer controlled_buffer_1
  assign controlled_buffer_2_out = multi_a_men_8b_2__1 ? _1 : 16'bz;  // Controlled_Buffer controlled_buffer_2
  assign controlled_buffer_3_out = multi_a_men_8b_3__0 ? _0 : 16'bz;  // Controlled_Buffer controlled_buffer_3
  assign controlled_buffer_4_out = multi_a_men_8b_3__1 ? _1 : 16'bz;  // Controlled_Buffer controlled_buffer_4
  Register #(.width(16)) register_2 (.D(Write_data), .en(and_2_out), .Q(_1), .clk(Clock), .clr(R));
  and and_2 (and_2_out, Enable_write, multi_a_men_8b_1__1);
  assign controlled_buffer_5_out = multi_a_men_8b_2__2 ? _2 : 16'bz;  // Controlled_Buffer controlled_buffer_5
  assign controlled_buffer_6_out = multi_a_men_8b_2__3 ? _3 : 16'bz;  // Controlled_Buffer controlled_buffer_6
  assign controlled_buffer_7_out = multi_a_men_8b_3__2 ? _2 : 16'bz;  // Controlled_Buffer controlled_buffer_7
  assign controlled_buffer_8_out = multi_a_men_8b_3__3 ? _3 : 16'bz;  // Controlled_Buffer controlled_buffer_8
  Register #(.width(16)) register_3 (.D(Write_data), .en(and_3_out), .Q(_2), .clk(Clock), .clr(R));
  and and_3 (and_3_out, Enable_write, multi_a_men_8b_1__2);
  assign controlled_buffer_9_out = multi_a_men_8b_2__4 ? _4 : 16'bz;  // Controlled_Buffer controlled_buffer_9
  assign controlled_buffer_10_out = multi_a_men_8b_2__5 ? _5 : 16'bz;  // Controlled_Buffer controlled_buffer_10
  assign controlled_buffer_11_out = multi_a_men_8b_3__4 ? _4 : 16'bz;  // Controlled_Buffer controlled_buffer_11
  assign controlled_buffer_12_out = multi_a_men_8b_3__5 ? _5 : 16'bz;  // Controlled_Buffer controlled_buffer_12
  and and_4 (and_4_out, Enable_write, multi_a_men_8b_1__3);
  assign controlled_buffer_13_out = multi_a_men_8b_2__6 ? _6 : 16'bz;  // Controlled_Buffer controlled_buffer_13
  assign controlled_buffer_14_out = multi_a_men_8b_2__7 ? _7 : 16'bz;  // Controlled_Buffer controlled_buffer_14
  assign controlled_buffer_15_out = multi_a_men_8b_3__6 ? _6 : 16'bz;  // Controlled_Buffer controlled_buffer_15
  assign controlled_buffer_16_out = multi_a_men_8b_3__7 ? _7 : 16'bz;  // Controlled_Buffer controlled_buffer_16
  Register #(.width(16)) register_4 (.D(Write_data), .en(and_4_out), .Q(_3), .clk(Clock), .clr(R));
  and and_5 (and_5_out, Enable_write, multi_a_men_8b_1__4);
  Register #(.width(16)) register_5 (.D(Write_data), .en(and_5_out), .Q(_4), .clk(Clock), .clr(R));
  Register #(.width(16)) register_6 (.D(Write_data), .en(and_6_out), .Q(_5), .clk(Clock), .clr(R));
  and and_6 (and_6_out, Enable_write, multi_a_men_8b_1__5);
  Or_8x16b or_8x16b_1 (
    ._7(controlled_buffer_1_out), ._6(controlled_buffer_2_out), ._5(controlled_buffer_5_out),
    ._4(controlled_buffer_6_out), ._3(controlled_buffer_9_out), ._2(controlled_buffer_10_out),
    ._1(controlled_buffer_13_out), ._0(controlled_buffer_14_out), .out_9(Out_1));
  Or_8x16b or_8x16b_2 (
    ._7(controlled_buffer_3_out), ._6(controlled_buffer_4_out), ._5(controlled_buffer_7_out),
    ._4(controlled_buffer_8_out), ._3(controlled_buffer_11_out), ._2(controlled_buffer_12_out),
    ._1(controlled_buffer_15_out), ._0(controlled_buffer_16_out), .out_9(Out_2));
  Register #(.width(16)) register_7 (.D(Write_data), .en(and_7_out), .Q(_6), .clk(Clock), .clr(R));
  and and_7 (and_7_out, Enable_write, multi_a_men_8b_1__6);
  and and_8 (and_8_out, Enable_write, multi_a_men_8b_1__7);
  Register #(.width(16)) register_8 (.D(Write_data), .en(and_8_out), .Q(_7), .clk(Clock), .clr(R));

  // Notes on the sheet:
  //   Rd: pull=down
  //   Rs: pull=down
  //   Out_1: pull=down
  //   Rt: pull=down
  //   R: pull=down
  //   Write_data: pull=down
  //   Out_2: pull=down
endmodule

module Memoria_grafica (
  input  R,
  input  Clock,
  input  [15:0] Write_data,
  input  Enable_write,
  input  [2:0] Address,
  output [15:0] Out_1,
  output [15:0] Out_2,
  output [15:0] Out_3,
  output [15:0] Out_4,
  output [15:0] Out_5,
  output [15:0] Out_6,
  output [15:0] Out_7,
  output [15:0] Out_8
);

  wire and_1_out, and_2_out, and_3_out, and_4_out, and_5_out, and_6_out, and_7_out, and_8_out,
       multi_a_men_8b_1__0, multi_a_men_8b_1__1, multi_a_men_8b_1__2, multi_a_men_8b_1__3,
       multi_a_men_8b_1__4, multi_a_men_8b_1__5, multi_a_men_8b_1__6, multi_a_men_8b_1__7;

  and and_1 (and_1_out, Enable_write, multi_a_men_8b_1__0);
  Multi_A_Men_8b multi_a_men_8b_1 (
    .in_1(Address), ._0(multi_a_men_8b_1__0), ._1(multi_a_men_8b_1__1), ._2(multi_a_men_8b_1__2),
    ._3(multi_a_men_8b_1__3), ._4(multi_a_men_8b_1__4), ._5(multi_a_men_8b_1__5), ._6(multi_a_men_8b_1__6),
    ._7(multi_a_men_8b_1__7));
  Register #(.width(16)) register_1 (.D(Write_data), .en(and_1_out), .Q(Out_1), .clk(Clock), .clr(R));
  Register #(.width(16)) register_2 (.D(Write_data), .en(and_2_out), .Q(Out_2), .clk(Clock), .clr(R));
  and and_2 (and_2_out, Enable_write, multi_a_men_8b_1__1);
  Register #(.width(16)) register_3 (.D(Write_data), .en(and_3_out), .Q(Out_3), .clk(Clock), .clr(R));
  and and_3 (and_3_out, Enable_write, multi_a_men_8b_1__2);
  and and_4 (and_4_out, Enable_write, multi_a_men_8b_1__3);
  Register #(.width(16)) register_4 (.D(Write_data), .en(and_4_out), .Q(Out_4), .clk(Clock), .clr(R));
  and and_5 (and_5_out, Enable_write, multi_a_men_8b_1__4);
  Register #(.width(16)) register_5 (.D(Write_data), .en(and_5_out), .Q(Out_5), .clk(Clock), .clr(R));
  Register #(.width(16)) register_6 (.D(Write_data), .en(and_6_out), .Q(Out_6), .clk(Clock), .clr(R));
  and and_6 (and_6_out, Enable_write, multi_a_men_8b_1__5);
  Register #(.width(16)) register_7 (.D(Write_data), .en(and_7_out), .Q(Out_7), .clk(Clock), .clr(R));
  and and_7 (and_7_out, Enable_write, multi_a_men_8b_1__6);
  and and_8 (and_8_out, Enable_write, multi_a_men_8b_1__7);
  Register #(.width(16)) register_8 (.D(Write_data), .en(and_8_out), .Q(Out_8), .clk(Clock), .clr(R));

  // Other names for the same wires on the sheet: _0[15:0] = Out_1; _1[15:0] = Out_2; _2[15:0] = Out_3;
  //   _3[15:0] = Out_4; _4[15:0] = Out_5; _5[15:0] = Out_6; _6[15:0] = Out_7; _7[15:0] = Out_8

  // Notes on the sheet:
  //   Out_2: pull=down
  //   R: pull=down
  //   Out_3: pull=down
  //   Write_data: pull=down
  //   Address: pull=down
  //   Out_1: pull=down
  //   Out_7: pull=down
  //   Out_8: pull=down
  //   Out_4: pull=down
  //   Out_5: pull=down
  //   Out_6: pull=down
endmodule

module Extensor_12_16 (
  input  [11:0] In,
  output [15:0] Out
);

  not not_1 (Out[15], 1'b1);

  assign Out[14:0] = {{3{Out[15]}}, In};

  // Notes on the sheet:
  //   Out: pull=down
endmodule

module Extensor_07_16 (
  input  [6:0] In,
  output [15:0] Out
);

  not not_1 (Out[15], 1'b1);

  assign Out[14:0] = {{8{Out[15]}}, In};

  // Notes on the sheet:
  //   Out: pull=down
endmodule

module sub (
  input  [15:0] A,
  input  [15:0] B,
  output [15:0] Out
);

  wire [15:0] add_16b_1_out_3, not_1_out;
  wire [15:15] not_2_out;

  assign not_1_out = ~B;  // NOT_Gate not_1, 16 bits wide
  not not_2 (not_2_out[15], 1'b1);
  Add_16b add_16b_1 (.A(not_1_out), .B({{15{not_2_out[15]}}, 1'b1}), .out_3(add_16b_1_out_3));
  Add_16b add_16b_2 (.A(A), .B(add_16b_1_out_3), .out_3(Out));

  // Notes on the sheet:
  //   A: pull=down
  //   Out: pull=down
  //   B: pull=down
endmodule

module Add_Simples (
  input  [15:0] A,
  input  [15:0] B,
  output [15:0] out_3
);

  wire add_1_of_out, add_2_of_out, add_3_of_out, add_4_of_out, add_5_of_out, add_6_of_out, add_7_of_out,
       add_8_of_out, add_9_of_out, add_10_of_out, add_11_of_out, add_12_of_out, add_13_of_out, add_14_of_out,
       add_15_of_out, add_16_of_out, button_1_out;

  Button button_1 (.out(button_1_out));
  Add add_1 (.B(B[0]), .A(A[0]), .Of_in(button_1_out), .Of_out(add_1_of_out), .Out(out_3[0]));
  Add add_2 (.B(B[1]), .A(A[1]), .Of_in(add_1_of_out), .Of_out(add_2_of_out), .Out(out_3[1]));
  Add add_3 (.B(B[3]), .A(A[3]), .Of_in(add_4_of_out), .Of_out(add_3_of_out), .Out(out_3[3]));
  Add add_4 (.B(B[2]), .A(A[2]), .Of_in(add_2_of_out), .Of_out(add_4_of_out), .Out(out_3[2]));
  Add add_5 (.B(B[4]), .A(A[4]), .Of_in(add_3_of_out), .Of_out(add_5_of_out), .Out(out_3[4]));
  Add add_6 (.B(B[6]), .A(A[6]), .Of_in(add_7_of_out), .Of_out(add_6_of_out), .Out(out_3[6]));
  Add add_7 (.B(B[5]), .A(A[5]), .Of_in(add_5_of_out), .Of_out(add_7_of_out), .Out(out_3[5]));
  Add add_8 (.B(B[7]), .A(A[7]), .Of_in(add_6_of_out), .Of_out(add_8_of_out), .Out(out_3[7]));
  Add add_9 (.B(B[9]), .A(A[9]), .Of_in(add_10_of_out), .Of_out(add_9_of_out), .Out(out_3[9]));
  Add add_10 (.B(B[8]), .A(A[8]), .Of_in(add_8_of_out), .Of_out(add_10_of_out), .Out(out_3[8]));
  Add add_11 (.B(B[10]), .A(A[10]), .Of_in(add_9_of_out), .Of_out(add_11_of_out), .Out(out_3[10]));
  Add add_12 (.B(B[11]), .A(A[11]), .Of_in(add_11_of_out), .Of_out(add_12_of_out), .Out(out_3[11]));
  Add add_13 (.B(B[12]), .A(A[12]), .Of_in(add_12_of_out), .Of_out(add_13_of_out), .Out(out_3[12]));
  Add add_14 (.B(B[13]), .A(A[13]), .Of_in(add_13_of_out), .Of_out(add_14_of_out), .Out(out_3[13]));
  Add add_15 (.B(B[14]), .A(A[14]), .Of_in(add_14_of_out), .Of_out(add_15_of_out), .Out(out_3[14]));
  Add add_16 (.B(B[15]), .A(A[15]), .Of_in(add_15_of_out), .Of_out(add_16_of_out), .Out(out_3[15]));
  LED led_1 (.in(add_16_of_out));

  // Notes on the sheet:
  //   A: pull=down
  //   out_3: pull=down
  //   B: pull=down
endmodule

module Shift_Left (
  input  [15:0] Shift,
  input  [15:0] Number,
  output [15:0] out_3
);

  wire [6:6] not_1_out;

  not not_1 (not_1_out[6], 1'b1);
  Multi_B_Men_16b multi_b_men_16b_1 (
    ._15({Number[0], {15{not_1_out[6]}}}), ._14({Number[1:0], {14{not_1_out[6]}}}),
    ._13({Number[2:0], {13{not_1_out[6]}}}), ._12({Number[3:0], {12{not_1_out[6]}}}),
    ._11({Number[4:0], {11{not_1_out[6]}}}), ._10({Number[5:0], {10{not_1_out[6]}}}),
    ._9({Number[6:0], {9{not_1_out[6]}}}), ._8({Number[7:0], {8{not_1_out[6]}}}),
    ._7({Number[8:0], {7{not_1_out[6]}}}), ._6({Number[9:0], {6{not_1_out[6]}}}),
    ._5({Number[10:0], {5{not_1_out[6]}}}), ._4({Number[11:0], {4{not_1_out[6]}}}),
    ._3({Number[12:0], {3{not_1_out[6]}}}), ._2({Number[13:0], {2{not_1_out[6]}}}),
    ._1({Number[14:0], not_1_out[6]}), .Adress(Shift[3:0]), .Out(out_3));  // open: _0

  // Notes on the sheet:
  //   Shift: pull=down
  //   out_3: pull=down
  //   Number: pull=down
endmodule

module Or_8x16b (
  input  [15:0] _7,
  input  [15:0] _6,
  input  [15:0] _5,
  input  [15:0] _4,
  input  [15:0] _3,
  input  [15:0] _2,
  input  [15:0] _1,
  input  [15:0] _0,
  output [15:0] out_9
);

  assign out_9 = _7 | _6 | _5 | _4 | _3 | _2 | _1 | _0;  // OR_Gate or_1, 16 bits wide

  // Notes on the sheet:
  //   _4: pull=down
  //   _5: pull=down
  //   _1: pull=down
  //   _6: pull=down
  //   _3: pull=down
  //   out_9: pull=down
  //   _2: pull=down
  //   _0: pull=down
  //   _7: pull=down
endmodule

module Shift_Right (
  input  [15:0] Shift,
  input  [15:0] Number,
  output [15:0] out_3
);

  wire [3:3] undriven;
  wire [15:15] not_1_out;

  not not_1 (not_1_out[15], 1'b1);
  Multi_B_Men_16b multi_b_men_16b_1 (
    ._15({{15{not_1_out[15]}}, Number[15]}), ._14({{14{not_1_out[15]}}, Number[15:14]}),
    ._13({{12{not_1_out[15]}}, undriven[3], Number[15:13]}), ._12({{12{not_1_out[15]}}, Number[15:12]}),
    ._11({{11{not_1_out[15]}}, Number[15:11]}), ._10({{10{not_1_out[15]}}, Number[15:10]}),
    ._9({{9{not_1_out[15]}}, Number[15:9]}), ._8({{8{not_1_out[15]}}, Number[15:8]}),
    ._7({{7{not_1_out[15]}}, Number[15:7]}), ._6({{6{not_1_out[15]}}, Number[15:6]}),
    ._5({{5{not_1_out[15]}}, Number[15:5]}), ._4({{4{not_1_out[15]}}, Number[15:4]}),
    ._3({{3{not_1_out[15]}}, Number[15:3]}), ._2({{2{not_1_out[15]}}, Number[15:2]}),
    ._1({not_1_out[15], Number[15:1]}), .Adress(Shift[3:0]), .Out(out_3));  // open: _0

  // Notes on the sheet:
  //   Number: pull=down
  //   Shift: pull=down
  //   out_3: pull=down
endmodule

module FlipFlopD (
  input  R,
  input  D,
  input  CK,
  input  S,
  output Q
);

  wire and_1_out, and_2_out, nor_2_out, not_1_out;

  not not_1 (not_1_out, D);
  and and_1 (and_1_out, not_1_out, CK);
  and and_2 (and_2_out, CK, D);
  nor nor_1 (Q, R, and_1_out, nor_2_out);
  nor nor_2 (nor_2_out, Q, and_2_out, S);

  // Notes on the sheet:
  //   D: pull=down
  //   Q: pull=down
  //   R: pull=down
  //   S: pull=down
  //   CK: pull=down
endmodule
